// Logisim project LAB1.circ as structural Verilog: 2 circuits, main circuit main
module main (
  input  A,
  input  B,
  input  Cin,
  output Sum,
  output Cout
);

  add_binary add_binary_1 (.A(A), .B(B), .Cin(Cin), .Sum(Sum), .Cout(Cout));
endmodule

module add_binary (
  input  A,
  input  B,
  input  Cin,
  output Sum,
  output Cout
);

  wire and_1_out, and_2_out, xor_1_out, xor_2_out;

  xor xor_1 (xor_1_out, A, B);
  xor xor_2 (xor_2_out, A, B);
  and and_1 (and_1_out, A, B);
  and and_2 (and_2_out, xor_1_out, Cin);
  xor xor_3 (Sum, xor_2_out, Cin);
  or or_1 (Cout, and_1_out, and_2_out);
endmodule
