// Logisim project Lab1plus.circ as structural Verilog: 3 circuits, main circuit main
module main (
  input  [7:0] in_1,
  input  [7:0] in_2,
  output out_3
);

  wire [7:0] adder_1_out;
  wire [8:0] add_eight_1_sum, xor_1_out;
  wire [8:8] adder_1_cout;

  Adder adder_1 (.a(in_1), .b(in_2), .out(adder_1_out), .cout(adder_1_cout[8]));  // open: cin
  add_eight add_eight_1 (.A(in_1), .B(in_2), .sum(add_eight_1_sum));
  // Probe on add_eight_1_sum
  assign xor_1_out = add_eight_1_sum ^ {adder_1_cout[8], adder_1_out};  // XOR_Gate xor_1, 9 bits wide
  // Probe on {adder_1_cout[8], adder_1_out}
  nor nor_1 (out_3, xor_1_out[0], xor_1_out[1], xor_1_out[2], xor_1_out[3], xor_1_out[4], xor_1_out[5], xor_1_out[6], xor_1_out[7], xor_1_out[8]);
endmodule

module add_binary (
  input  A,
  input  B,
  input  Cin,
  output Sum,
  output Cout
);

  wire and_1_out, and_2_out, xor_1_out, xor_2_out;

  xor xor_1 (xor_1_out, A, B);
  xor xor_2 (xor_2_out, A, B);
  and and_1 (and_1_out, A, B);
  and and_2 (and_2_out, xor_1_out, Cin);
  xor xor_3 (Sum, xor_2_out, Cin);
  or or_1 (Cout, and_1_out, and_2_out);
endmodule

module add_eight (
  input  [7:0] A,
  input  [7:0] B,
  output [8:0] sum
);

  wire add_binary_1_cout, add_binary_2_cout, add_binary_3_cout, add_binary_4_cout, add_binary_5_cout,
       add_binary_6_cout, add_binary_7_cout;

  add_binary add_binary_1 (.A(A[0]), .B(B[0]), .Cin(1'b0), .Sum(sum[0]), .Cout(add_binary_1_cout));
  add_binary add_binary_2 (.A(A[2]), .B(B[1]), .Cin(add_binary_1_cout), .Sum(sum[1]), .Cout(add_binary_2_cout));
  add_binary add_binary_3 (.A(A[3]), .B(B[2]), .Cin(add_binary_2_cout), .Sum(sum[2]), .Cout(add_binary_3_cout));
  add_binary add_binary_4 (.A(A[4]), .B(B[3]), .Cin(add_binary_3_cout), .Sum(sum[3]), .Cout(add_binary_4_cout));
  add_binary add_binary_5 (.A(A[5]), .B(B[4]), .Cin(add_binary_4_cout), .Sum(sum[4]), .Cout(add_binary_5_cout));
  add_binary add_binary_6 (.A(A[6]), .B(B[5]), .Cin(add_binary_5_cout), .Sum(sum[5]), .Cout(add_binary_6_cout));
  add_binary add_binary_7 (.A(A[1]), .B(B[6]), .Cin(add_binary_6_cout), .Sum(sum[6]), .Cout(add_binary_7_cout));
  add_binary add_binary_8 (.A(A[7]), .B(B[7]), .Cin(add_binary_7_cout), .Sum(sum[7]), .Cout(sum[8]));
endmodule
