// Logisim project LAB_2 - 副本.circ as structural Verilog
module ALU (
  input  [15:0] A,
  input  [15:0] B,
  input  [2:0] Control_Lines,
  output [3:0] FLAG,
  output [15:0] C
);

  wire comparator_1_eq, comparator_1_lt, comparator_2_eq, comparator_2_lt, comparator_3_eq, comparator_3_lt,
       comparator_4_eq, comparator_4_lt, xnor_1_out, xor_1_out;
  wire [15:0] adder_1_out, and_1_out, asr_1_asrout, ls_l_1_lsl, ls_r_1_lsr, multiplexer_1_out, not_1_out,
       not_2_out, or_1_out;

  Multiplexer #(.width(16)) multiplexer_1 (.in0(B), .in1(not_1_out), .out(multiplexer_1_out), .sel(Control_Lines[2]));
  assign not_1_out = ~B;  // NOT_Gate not_1, 16 bits wide
  Comparator #(.width(16)) comparator_1 (.a(B), .b(A), .eq(comparator_1_eq), .lt(comparator_1_lt));  // open: gt
  Adder #(.width(16)) adder_1 (.a(A), .b(multiplexer_1_out), .out(adder_1_out), .cin(Control_Lines[2]), .cout(FLAG[1]));
  assign and_1_out = A & B;  // AND_Gate and_1, 16 bits wide
  assign or_1_out = A | B;  // OR_Gate or_1, 16 bits wide
  assign not_2_out = ~or_1_out;  // NOT_Gate not_2, 16 bits wide
  LS_L ls_l_1 (.A(A), .B(B[1:0]), .LSL(ls_l_1_lsl));
  LS_R ls_r_1 (.A(A), .B(B[1:0]), .LSR(ls_r_1_lsr));
  ASR asr_1 (.A(A), .B(B[1:0]), .ASRout(asr_1_asrout));
  xnor xnor_1 (xnor_1_out, B[15], A[15]);
  ExactlyOne xor_1 (.out(xor_1_out), .in0(B[15]), .in1(adder_1_out[15]), .in2(A[15]));
  Comparator #(.width(16)) comparator_2 (
    .a(ls_l_1_lsl), .b({16{1'b0}}), .eq(comparator_2_eq), .lt(comparator_2_lt));  // open: gt
  Comparator #(.width(16)) comparator_3 (
    .a(ls_r_1_lsr), .b({16{1'b0}}), .eq(comparator_3_eq), .lt(comparator_3_lt));  // open: gt
  Comparator #(.width(16)) comparator_4 (
    .a(asr_1_asrout), .b({16{1'b0}}), .eq(comparator_4_eq), .lt(comparator_4_lt));  // open: gt
  and and_2 (FLAG[0], xnor_1_out, xor_1_out);
  Multiplexer #(.select(3), .width(16)) multiplexer_2 (
    .in0(adder_1_out), .in1(adder_1_out), .in2(and_1_out), .in3(or_1_out), .in4(not_2_out), .in5(ls_l_1_lsl),
    .in6(ls_r_1_lsr), .in7(asr_1_asrout), .out(C), .sel(Control_Lines));
  or or_2 (FLAG[3], comparator_1_lt, comparator_2_lt, comparator_3_lt, comparator_4_lt);
  or or_3 (FLAG[2], comparator_2_eq, comparator_3_eq, comparator_4_eq, comparator_1_eq);
endmodule

module LS_L (
  input  [15:0] A,
  input  [1:0] B,
  output [15:0] LSL
);

  wire multiplexer_1_out, multiplexer_2_out, multiplexer_3_out, multiplexer_4_out, multiplexer_5_out,
       multiplexer_6_out, multiplexer_7_out, multiplexer_8_out, multiplexer_9_out, multiplexer_10_out,
       multiplexer_11_out, multiplexer_12_out, multiplexer_13_out, multiplexer_14_out, multiplexer_15_out,
       multiplexer_16_out;

  Multiplexer multiplexer_1 (.in0(A[0]), .in1(A[1]), .out(multiplexer_1_out), .sel(B[0]));
  Multiplexer multiplexer_2 (.in0(A[1]), .in1(A[2]), .out(multiplexer_2_out), .sel(B[0]));
  Multiplexer multiplexer_3 (.in0(A[2]), .in1(A[3]), .out(multiplexer_3_out), .sel(B[0]));
  Multiplexer multiplexer_4 (.in0(A[3]), .in1(A[4]), .out(multiplexer_4_out), .sel(B[0]));
  Multiplexer multiplexer_5 (.in0(A[4]), .in1(A[5]), .out(multiplexer_5_out), .sel(B[0]));
  Multiplexer multiplexer_6 (.in0(A[5]), .in1(A[6]), .out(multiplexer_6_out), .sel(B[0]));
  Multiplexer multiplexer_7 (.in0(A[6]), .in1(A[7]), .out(multiplexer_7_out), .sel(B[0]));
  Multiplexer multiplexer_8 (.in0(A[7]), .in1(A[8]), .out(multiplexer_8_out), .sel(B[0]));
  Multiplexer multiplexer_9 (.in0(A[8]), .in1(A[9]), .out(multiplexer_9_out), .sel(B[0]));
  Multiplexer multiplexer_10 (.in0(A[9]), .in1(A[10]), .out(multiplexer_10_out), .sel(B[0]));
  Multiplexer multiplexer_11 (.in0(A[10]), .in1(A[11]), .out(multiplexer_11_out), .sel(B[0]));
  Multiplexer multiplexer_12 (.in0(A[11]), .in1(A[12]), .out(multiplexer_12_out), .sel(B[0]));
  Multiplexer multiplexer_13 (.in0(A[12]), .in1(A[13]), .out(multiplexer_13_out), .sel(B[0]));
  Multiplexer multiplexer_14 (.in0(A[13]), .in1(A[14]), .out(multiplexer_14_out), .sel(B[0]));
  Multiplexer multiplexer_15 (.in0(A[14]), .in1(A[15]), .out(multiplexer_15_out), .sel(B[0]));
  Multiplexer multiplexer_16 (.in0(A[15]), .in1(1'b0), .out(multiplexer_16_out), .sel(B[0]));
  Multiplexer multiplexer_17 (.in0(multiplexer_1_out), .in1(multiplexer_3_out), .out(LSL[0]), .sel(B[1]));
  Multiplexer multiplexer_18 (.in0(multiplexer_2_out), .in1(multiplexer_4_out), .out(LSL[1]), .sel(B[1]));
  Multiplexer multiplexer_19 (.in0(multiplexer_3_out), .in1(multiplexer_5_out), .out(LSL[2]), .sel(B[1]));
  Multiplexer multiplexer_20 (.in0(multiplexer_4_out), .in1(multiplexer_6_out), .out(LSL[3]), .sel(B[1]));
  Multiplexer multiplexer_21 (.in0(multiplexer_5_out), .in1(multiplexer_7_out), .out(LSL[4]), .sel(B[1]));
  Multiplexer multiplexer_22 (.in0(multiplexer_6_out), .in1(multiplexer_8_out), .out(LSL[5]), .sel(B[1]));
  Multiplexer multiplexer_23 (.in0(multiplexer_7_out), .in1(multiplexer_9_out), .out(LSL[6]), .sel(B[1]));
  Multiplexer multiplexer_24 (.in0(multiplexer_8_out), .in1(multiplexer_10_out), .out(LSL[7]), .sel(B[1]));
  Multiplexer multiplexer_25 (.in0(multiplexer_9_out), .in1(multiplexer_11_out), .out(LSL[8]), .sel(B[1]));
  Multiplexer multiplexer_26 (.in0(multiplexer_10_out), .in1(multiplexer_12_out), .out(LSL[9]), .sel(B[1]));
  Multiplexer multiplexer_27 (.in0(multiplexer_11_out), .in1(multiplexer_13_out), .out(LSL[10]), .sel(B[1]));
  Multiplexer multiplexer_28 (.in0(multiplexer_12_out), .in1(multiplexer_14_out), .out(LSL[11]), .sel(B[1]));
  Multiplexer multiplexer_29 (.in0(multiplexer_13_out), .in1(multiplexer_15_out), .out(LSL[12]), .sel(B[1]));
  Multiplexer multiplexer_30 (.in0(multiplexer_14_out), .in1(multiplexer_16_out), .out(LSL[13]), .sel(B[1]));
  Multiplexer multiplexer_31 (.in0(multiplexer_15_out), .in1(1'b0), .out(LSL[14]), .sel(B[1]));
  Multiplexer multiplexer_32 (.in0(multiplexer_16_out), .in1(1'b0), .out(LSL[15]), .sel(B[1]));
endmodule

module LS_R (
  input  [15:0] A,
  input  [1:0] B,
  output [15:0] LSR
);

  wire multiplexer_1_out, multiplexer_2_out, multiplexer_3_out, multiplexer_4_out, multiplexer_5_out,
       multiplexer_6_out, multiplexer_7_out, multiplexer_8_out, multiplexer_9_out, multiplexer_10_out,
       multiplexer_11_out, multiplexer_12_out, multiplexer_13_out, multiplexer_14_out, multiplexer_15_out,
       multiplexer_16_out;

  Multiplexer multiplexer_1 (.in0(A[15]), .in1(A[14]), .out(multiplexer_1_out), .sel(B[0]));
  Multiplexer multiplexer_2 (.in0(A[14]), .in1(A[13]), .out(multiplexer_2_out), .sel(B[0]));
  Multiplexer multiplexer_3 (.in0(A[13]), .in1(A[12]), .out(multiplexer_3_out), .sel(B[0]));
  Multiplexer multiplexer_4 (.in0(A[12]), .in1(A[11]), .out(multiplexer_4_out), .sel(B[0]));
  Multiplexer multiplexer_5 (.in0(A[11]), .in1(A[10]), .out(multiplexer_5_out), .sel(B[0]));
  Multiplexer multiplexer_6 (.in0(A[10]), .in1(A[9]), .out(multiplexer_6_out), .sel(B[0]));
  Multiplexer multiplexer_7 (.in0(A[9]), .in1(A[8]), .out(multiplexer_7_out), .sel(B[0]));
  Multiplexer multiplexer_8 (.in0(A[8]), .in1(A[7]), .out(multiplexer_8_out), .sel(B[0]));
  Multiplexer multiplexer_9 (.in0(A[7]), .in1(A[6]), .out(multiplexer_9_out), .sel(B[0]));
  Multiplexer multiplexer_10 (.in0(A[6]), .in1(A[5]), .out(multiplexer_10_out), .sel(B[0]));
  Multiplexer multiplexer_11 (.in0(A[5]), .in1(A[4]), .out(multiplexer_11_out), .sel(B[0]));
  Multiplexer multiplexer_12 (.in0(A[4]), .in1(A[3]), .out(multiplexer_12_out), .sel(B[0]));
  Multiplexer multiplexer_13 (.in0(A[3]), .in1(A[2]), .out(multiplexer_13_out), .sel(B[0]));
  Multiplexer multiplexer_14 (.in0(A[2]), .in1(A[1]), .out(multiplexer_14_out), .sel(B[0]));
  Multiplexer multiplexer_15 (.in0(A[1]), .in1(A[0]), .out(multiplexer_15_out), .sel(B[0]));
  Multiplexer multiplexer_16 (.in0(A[0]), .in1(1'b0), .out(multiplexer_16_out), .sel(B[0]));
  Multiplexer multiplexer_17 (.in0(multiplexer_1_out), .in1(multiplexer_3_out), .out(LSR[15]), .sel(B[1]));
  Multiplexer multiplexer_18 (.in0(multiplexer_2_out), .in1(multiplexer_4_out), .out(LSR[14]), .sel(B[1]));
  Multiplexer multiplexer_19 (.in0(multiplexer_3_out), .in1(multiplexer_5_out), .out(LSR[13]), .sel(B[1]));
  Multiplexer multiplexer_20 (.in0(multiplexer_4_out), .in1(multiplexer_6_out), .out(LSR[12]), .sel(B[1]));
  Multiplexer multiplexer_21 (.in0(multiplexer_5_out), .in1(multiplexer_7_out), .out(LSR[11]), .sel(B[1]));
  Multiplexer multiplexer_22 (.in0(multiplexer_6_out), .in1(multiplexer_8_out), .out(LSR[10]), .sel(B[1]));
  Multiplexer multiplexer_23 (.in0(multiplexer_7_out), .in1(multiplexer_9_out), .out(LSR[9]), .sel(B[1]));
  Multiplexer multiplexer_24 (.in0(multiplexer_8_out), .in1(multiplexer_10_out), .out(LSR[8]), .sel(B[1]));
  Multiplexer multiplexer_25 (.in0(multiplexer_9_out), .in1(multiplexer_11_out), .out(LSR[7]), .sel(B[1]));
  Multiplexer multiplexer_26 (.in0(multiplexer_10_out), .in1(multiplexer_12_out), .out(LSR[6]), .sel(B[1]));
  Multiplexer multiplexer_27 (.in0(multiplexer_11_out), .in1(multiplexer_13_out), .out(LSR[5]), .sel(B[1]));
  Multiplexer multiplexer_28 (.in0(multiplexer_12_out), .in1(multiplexer_14_out), .out(LSR[4]), .sel(B[1]));
  Multiplexer multiplexer_29 (.in0(multiplexer_13_out), .in1(multiplexer_15_out), .out(LSR[3]), .sel(B[1]));
  Multiplexer multiplexer_30 (.in0(multiplexer_14_out), .in1(multiplexer_16_out), .out(LSR[2]), .sel(B[1]));
  Multiplexer multiplexer_31 (.in0(multiplexer_15_out), .in1(1'b0), .out(LSR[1]), .sel(B[1]));
  Multiplexer multiplexer_32 (.in0(multiplexer_16_out), .in1(1'b0), .out(LSR[0]), .sel(B[1]));
endmodule

module ASR (
  input  [15:0] A,
  input  [1:0] B,
  output [15:0] ASRout
);

  wire multiplexer_1_out, multiplexer_2_out, multiplexer_3_out, multiplexer_4_out, multiplexer_5_out,
       multiplexer_6_out, multiplexer_7_out, multiplexer_8_out, multiplexer_9_out, multiplexer_10_out,
       multiplexer_11_out, multiplexer_12_out, multiplexer_13_out, multiplexer_14_out, multiplexer_15_out,
       multiplexer_16_out;

  Multiplexer multiplexer_1 (.in0(A[15]), .in1(A[14]), .out(multiplexer_1_out), .sel(B[0]));
  Multiplexer multiplexer_2 (.in0(A[14]), .in1(A[13]), .out(multiplexer_2_out), .sel(B[0]));
  Multiplexer multiplexer_3 (.in0(A[13]), .in1(A[12]), .out(multiplexer_3_out), .sel(B[0]));
  Multiplexer multiplexer_4 (.in0(A[12]), .in1(A[11]), .out(multiplexer_4_out), .sel(B[0]));
  Multiplexer multiplexer_5 (.in0(A[11]), .in1(A[10]), .out(multiplexer_5_out), .sel(B[0]));
  Multiplexer multiplexer_6 (.in0(A[10]), .in1(A[9]), .out(multiplexer_6_out), .sel(B[0]));
  Multiplexer multiplexer_7 (.in0(A[9]), .in1(A[8]), .out(multiplexer_7_out), .sel(B[0]));
  Multiplexer multiplexer_8 (.in0(A[8]), .in1(A[7]), .out(multiplexer_8_out), .sel(B[0]));
  Multiplexer multiplexer_9 (.in0(A[7]), .in1(A[6]), .out(multiplexer_9_out), .sel(B[0]));
  Multiplexer multiplexer_10 (.in0(A[6]), .in1(A[5]), .out(multiplexer_10_out), .sel(B[0]));
  Multiplexer multiplexer_11 (.in0(A[5]), .in1(A[4]), .out(multiplexer_11_out), .sel(B[0]));
  Multiplexer multiplexer_12 (.in0(A[4]), .in1(A[3]), .out(multiplexer_12_out), .sel(B[0]));
  Multiplexer multiplexer_13 (.in0(A[3]), .in1(A[2]), .out(multiplexer_13_out), .sel(B[0]));
  Multiplexer multiplexer_14 (.in0(A[2]), .in1(A[1]), .out(multiplexer_14_out), .sel(B[0]));
  Multiplexer multiplexer_15 (.in0(A[1]), .in1(A[0]), .out(multiplexer_15_out), .sel(B[0]));
  Multiplexer multiplexer_16 (.in0(A[0]), .in1(A[15]), .out(multiplexer_16_out), .sel(B[0]));
  Multiplexer multiplexer_17 (.in0(multiplexer_1_out), .in1(multiplexer_3_out), .out(ASRout[15]), .sel(B[1]));
  Multiplexer multiplexer_18 (.in0(multiplexer_2_out), .in1(multiplexer_4_out), .out(ASRout[14]), .sel(B[1]));
  Multiplexer multiplexer_19 (.in0(multiplexer_3_out), .in1(multiplexer_5_out), .out(ASRout[13]), .sel(B[1]));
  Multiplexer multiplexer_20 (.in0(multiplexer_4_out), .in1(multiplexer_6_out), .out(ASRout[12]), .sel(B[1]));
  Multiplexer multiplexer_21 (.in0(multiplexer_5_out), .in1(multiplexer_7_out), .out(ASRout[11]), .sel(B[1]));
  Multiplexer multiplexer_22 (.in0(multiplexer_6_out), .in1(multiplexer_8_out), .out(ASRout[10]), .sel(B[1]));
  Multiplexer multiplexer_23 (.in0(multiplexer_7_out), .in1(multiplexer_9_out), .out(ASRout[9]), .sel(B[1]));
  Multiplexer multiplexer_24 (.in0(multiplexer_8_out), .in1(multiplexer_10_out), .out(ASRout[8]), .sel(B[1]));
  Multiplexer multiplexer_25 (.in0(multiplexer_9_out), .in1(multiplexer_11_out), .out(ASRout[7]), .sel(B[1]));
  Multiplexer multiplexer_26 (.in0(multiplexer_10_out), .in1(multiplexer_12_out), .out(ASRout[6]), .sel(B[1]));
  Multiplexer multiplexer_27 (.in0(multiplexer_11_out), .in1(multiplexer_13_out), .out(ASRout[5]), .sel(B[1]));
  Multiplexer multiplexer_28 (.in0(multiplexer_12_out), .in1(multiplexer_14_out), .out(ASRout[4]), .sel(B[1]));
  Multiplexer multiplexer_29 (.in0(multiplexer_13_out), .in1(multiplexer_15_out), .out(ASRout[3]), .sel(B[1]));
  Multiplexer multiplexer_30 (.in0(multiplexer_14_out), .in1(multiplexer_16_out), .out(ASRout[2]), .sel(B[1]));
  Multiplexer multiplexer_31 (.in0(multiplexer_15_out), .in1(A[15]), .out(ASRout[1]), .sel(B[1]));
  Multiplexer multiplexer_32 (.in0(multiplexer_16_out), .in1(A[15]), .out(ASRout[0]), .sel(B[1]));
endmodule

module Register_File (
  input  [2:0] addr_A,
  input  [2:0] addr_B,
  input  [2:0] addr_C,
  input  we,
  input  [15:0] C,
  output [15:0] A,
  output [15:0] B
);

  wire and_1_out, and_2_out, and_3_out, and_4_out, and_5_out, and_6_out, and_7_out, and_8_out,
       decoder_1_out0, decoder_1_out1, decoder_1_out2, decoder_1_out3, decoder_1_out4, decoder_1_out5,
       decoder_1_out6, decoder_1_out7;
  wire [15:0] R0_q, R1_q, R2_q, R3_q, R4_q, R5_q, R6_q, R7_q;

  Decoder #(.select(3)) decoder_1 (
    .out0(decoder_1_out0), .out1(decoder_1_out1), .out2(decoder_1_out2), .out3(decoder_1_out3),
    .out4(decoder_1_out4), .out5(decoder_1_out5), .out6(decoder_1_out6), .out7(decoder_1_out7), .sel(addr_C));  // open: en
  and and_1 (and_1_out, decoder_1_out0, we);
  and and_2 (and_2_out, decoder_1_out1, we);
  and and_3 (and_3_out, decoder_1_out2, we);
  and and_4 (and_4_out, decoder_1_out3, we);
  and and_5 (and_5_out, decoder_1_out4, we);
  and and_6 (and_6_out, decoder_1_out5, we);
  and and_7 (and_7_out, decoder_1_out6, we);
  and and_8 (and_8_out, decoder_1_out7, we);
  Register #(.width(16)) R0 (.D(C), .en(and_1_out), .Q(R0_q));  // open: clk, clr
  Register #(.width(16)) R1 (.D(C), .en(and_2_out), .Q(R1_q));  // open: clk, clr
  Register #(.width(16)) R2 (.D(C), .en(and_3_out), .Q(R2_q));  // open: clk, clr
  Register #(.width(16)) R3 (.D(C), .en(and_4_out), .Q(R3_q));  // open: clk, clr
  Register #(.width(16)) R4 (.D(C), .en(and_5_out), .Q(R4_q));  // open: clk, clr
  Register #(.width(16)) R5 (.D(C), .en(and_6_out), .Q(R5_q));  // open: clk, clr
  Register #(.width(16)) R6 (.D(C), .en(and_7_out), .Q(R6_q));  // open: clk, clr
  Register #(.width(16)) R7 (.D(C), .en(and_8_out), .Q(R7_q));  // open: clk, clr
  Multiplexer #(.select(3), .width(16)) multiplexer_1 (
    .in0(R0_q), .in1(R1_q), .in2(R2_q), .in3(R3_q), .in4(R4_q), .in5(R5_q), .in6(R6_q), .in7(R7_q), .out(A),
    .sel(addr_A));
  Multiplexer #(.select(3), .width(16)) multiplexer_2 (
    .in0(R0_q), .in1(R1_q), .in2(R2_q), .in3(R3_q), .in4(R4_q), .in5(R5_q), .in6(R6_q), .in7(R7_q), .out(B),
    .sel(addr_B));
endmodule
