// Logisim project cpu(3).circ as structural Verilog: 9 circuits, main circuit CPU
module CPU (
  output [47:0] cpu_out,
  output halt
);

  wire alu_1_negative, alu_1_overflow, alu_1_zero, and_1_out, clk_out, decoder_1_out1, decoder_1_out2,
       decoder_1_out3, fsm_1_ir_we, fsm_1_mem_write, fsm_1_pc_we, fsm_1_ra_we, fsm_1_rb_we, fsm_1_rd_we,
       fsm_1_rf_we, fsm_1_rw_we, fsm_1_rz_we, multiplexer_3_out, reset_out, znv_1_result;
  wire [2:0] multiplexer_4_out, multiplexer_5_out;
  wire [15:0] adder_1_out, alu_1_c, bit_extender_1_out, bit_extender_2_out, InsMem_data, multiplexer_1_out,
       multiplexer_2_out, multiplexer_6_out, RA_q, ram_1_dout, RB_q, RD_q, registerfile_1_a,
       registerfile_1_b, RW_q;

  ZNV znv_1 (.Conditon(cpu_out[29:27]), .Z(alu_1_zero), .N(alu_1_negative), .V(alu_1_overflow), .Result(znv_1_result));
  and and_1 (and_1_out, decoder_1_out1, fsm_1_rd_we, znv_1_result);
  assign bit_extender_1_out = {{13{cpu_out[25]}}, cpu_out[25:23]};  // Bit_Extender bit_extender_1
  Clock clk (.out(clk_out));
  Button reset (.out(reset_out));
  Multiplexer #(.width(16)) multiplexer_1 (
    .in0(16'h1), .in1(bit_extender_1_out), .out(multiplexer_1_out), .sel(and_1_out));
  Register #(.width(16)) PC (.D(adder_1_out), .en(fsm_1_pc_we), .clk(clk_out), .Q(cpu_out[47:32]), .clr(reset_out));
  Adder #(.width(16)) adder_1 (.a(cpu_out[47:32]), .b(multiplexer_1_out), .out(adder_1_out));  // open: cin, cout
  ROM #(.addrWidth(16), .dataWidth(16)) InsMem (.addr(cpu_out[47:32]), .data(InsMem_data));
  FSM fsm_1 (
    .CLK(clk_out), .OP(cpu_out[31:30]), .Branch(and_1_out), .ir_we(fsm_1_ir_we), .pc_we(fsm_1_pc_we),
    .ra_we(fsm_1_ra_we), .rb_we(fsm_1_rb_we), .rz_we(fsm_1_rz_we), .rd_we(fsm_1_rd_we), .rw_we(fsm_1_rw_we),
    .rf_we(fsm_1_rf_we), .Mem_write(fsm_1_mem_write));
  RegisterFile registerfile_1 (
    .C(RW_q), .Addr_C(cpu_out[25:23]), .we(fsm_1_rf_we), .Addr_B(multiplexer_5_out), .Addr_A(cpu_out[22:20]),
    .clk(clk_out), .reset(reset_out), .A(registerfile_1_a), .B(registerfile_1_b));
  Register #(.width(16)) RA (.D(registerfile_1_a), .en(fsm_1_ra_we), .clk(clk_out), .Q(RA_q), .clr(reset_out));
  Register #(.width(16)) RB (.D(registerfile_1_b), .en(fsm_1_rb_we), .clk(clk_out), .Q(RB_q), .clr(reset_out));
  Register #(.width(16)) IR (.D(InsMem_data), .en(fsm_1_ir_we), .clk(clk_out), .Q(cpu_out[31:16]), .clr(reset_out));
  Multiplexer #(.width(16)) multiplexer_2 (
    .in0(RB_q), .in1(bit_extender_2_out), .out(multiplexer_2_out), .sel(multiplexer_3_out));
  Multiplexer multiplexer_3 (.in0(cpu_out[26]), .in1(1'b1), .out(multiplexer_3_out), .sel(decoder_1_out3));
  Multiplexer #(.width(3)) multiplexer_4 (
    .in0(cpu_out[29:27]), .in1(3'b001), .out(multiplexer_4_out), .sel(decoder_1_out1));
  Multiplexer #(.width(3)) multiplexer_5 (
    .in0(cpu_out[18:16]), .in1(cpu_out[25:23]), .out(multiplexer_5_out), .sel(decoder_1_out3));
  Register #(.width(16)) RZ (.D(alu_1_c), .en(fsm_1_rz_we), .clk(clk_out), .Q(cpu_out[15:0]), .clr(reset_out));
  ALU alu_1 (
    .A(RA_q), .B(multiplexer_2_out), .fun(multiplexer_4_out), .C(alu_1_c), .overflow(alu_1_overflow),
    .zero(alu_1_zero), .negative(alu_1_negative));  // open: carry
  Register #(.width(16)) RD (.D(RB_q), .en(fsm_1_rd_we), .clk(clk_out), .Q(RD_q), .clr(reset_out));
  Comparator #(.width(16)) comparator_1 (.a(cpu_out[31:16]), .b(16'h4380), .eq(halt));  // open: gt, lt
  Multiplexer #(.width(16)) multiplexer_6 (
    .in0(cpu_out[15:0]), .in1(ram_1_dout), .out(multiplexer_6_out), .sel(decoder_1_out2));
  Register #(.width(16)) RW (.D(multiplexer_6_out), .en(fsm_1_rw_we), .clk(clk_out), .Q(RW_q), .clr(reset_out));
  Decoder #(.enable("false"), .select(2)) decoder_1 (
    .out1(decoder_1_out1), .out2(decoder_1_out2), .out3(decoder_1_out3), .sel(cpu_out[31:30]));  // open: out0
  assign bit_extender_2_out = {{12{cpu_out[19]}}, cpu_out[19:16]};  // Bit_Extender bit_extender_2
  RAM #(.addrWidth(16), .dataWidth(16), .enables("line")) ram_1 (
    .addr(cpu_out[15:0]), .we(fsm_1_mem_write), .clk(clk_out), .din(RD_q), .dout(ram_1_dout));

  // Notes on the sheet:
  //   IMux
  //   OPcode
  //   ALU
  //   Src.Reg1
  //   Dest.Reg
  //   I
  //   MMux
  //   Src.Op2
endmodule

module ALU (
  input  [15:0] A,
  input  [15:0] B,
  input  [2:0] fun,
  output overflow,
  output carry,
  output zero,
  output [15:0] C,
  output negative
);

  wire xnor_1_out, xor_1_out, xor_2_out;
  wire [15:0] adder_1_out, and_1_out, asr_1_asro, lsl_1_lslo, lsr_1_lsro, multiplexer_1_out, nor_1_out,
       not_1_out, or_1_out;

  Multiplexer #(.width(16)) multiplexer_1 (.in0(B), .in1(not_1_out), .out(multiplexer_1_out), .sel(fun[0]));
  assign not_1_out = ~B;  // NOT_Gate not_1, 16 bits wide
  Adder #(.width(16)) adder_1 (.a(A), .b(multiplexer_1_out), .out(adder_1_out), .cin(fun[0]), .cout(carry));
  assign and_1_out = A & B;  // AND_Gate and_1, 16 bits wide
  assign or_1_out = A | B;  // OR_Gate or_1, 16 bits wide
  assign nor_1_out = ~(A | B);  // NOR_Gate nor_1, 16 bits wide
  ASR asr_1 (.A(A), .B(B), .ASRO(asr_1_asro));
  xor xor_1 (xor_1_out, multiplexer_1_out[15], adder_1_out[15]);
  xor xor_2 (xor_2_out, A[15], adder_1_out[15]);
  xnor xnor_1 (xnor_1_out, A[15], multiplexer_1_out[15]);
  LSL lsl_1 (.A(A), .B(B), .LSLO(lsl_1_lslo));
  LSR lsr_1 (.A(A), .B(B), .LSRO(lsr_1_lsro));
  and and_2 (overflow, xor_2_out, xor_1_out, xnor_1_out);
  Multiplexer #(.select(3), .width(16)) multiplexer_2 (
    .in0(adder_1_out), .in1(adder_1_out), .in2(and_1_out), .in3(or_1_out), .in4(nor_1_out), .in5(lsl_1_lslo),
    .in6(lsr_1_lsro), .in7(asr_1_asro), .out(C), .sel(fun));
  nor nor_2 (zero, C[0], C[1], C[2], C[3], C[4], C[5], C[6], C[7], C[8], C[9], C[10], C[11], C[12], C[13], C[14], C[15]);

  assign negative = C[15];
endmodule

module RegisterFile (
  input  [15:0] C,
  input  [2:0] Addr_C,
  input  we,
  input  [2:0] Addr_B,
  input  [2:0] Addr_A,
  input  clk,
  input  reset,
  output [15:0] A,
  output [15:0] B
);

  wire and_1_out, and_2_out, and_3_out, and_4_out, and_5_out, and_6_out, and_7_out, and_8_out,
       decoder_1_out0, decoder_1_out1, decoder_1_out2, decoder_1_out3, decoder_1_out4, decoder_1_out5,
       decoder_1_out6, decoder_1_out7;
  wire [15:0] R0_q, R1_q, R2_q, R3_q, R4_q, R5_q, R6_q, R7_q;

  Decoder #(.enable("false"), .select(3)) decoder_1 (
    .out0(decoder_1_out0), .out1(decoder_1_out1), .out2(decoder_1_out2), .out3(decoder_1_out3),
    .out4(decoder_1_out4), .out5(decoder_1_out5), .out6(decoder_1_out6), .out7(decoder_1_out7), .sel(Addr_C));
  and and_1 (and_1_out, decoder_1_out0, we);
  and and_2 (and_2_out, decoder_1_out1, we);
  and and_3 (and_3_out, decoder_1_out2, we);
  and and_4 (and_4_out, decoder_1_out3, we);
  and and_5 (and_5_out, decoder_1_out4, we);
  and and_6 (and_6_out, decoder_1_out5, we);
  and and_7 (and_7_out, decoder_1_out6, we);
  and and_8 (and_8_out, decoder_1_out7, we);
  Register #(.width(16)) R0 (.D(C), .en(and_1_out), .clk(clk), .Q(R0_q), .clr(reset));
  Register #(.width(16)) R1 (.D(C), .en(and_2_out), .clk(clk), .Q(R1_q), .clr(reset));
  Register #(.width(16)) R2 (.D(C), .en(and_3_out), .clk(clk), .Q(R2_q), .clr(reset));
  Register #(.width(16)) R3 (.D(C), .en(and_4_out), .clk(clk), .Q(R3_q), .clr(reset));
  Register #(.width(16)) R4 (.D(C), .en(and_5_out), .clk(clk), .Q(R4_q), .clr(reset));
  Register #(.width(16)) R5 (.D(C), .en(and_6_out), .clk(clk), .Q(R5_q), .clr(reset));
  Register #(.width(16)) R6 (.D(C), .en(and_7_out), .clk(clk), .Q(R6_q), .clr(reset));
  Register #(.width(16)) R7 (.D(C), .en(and_8_out), .clk(clk), .Q(R7_q), .clr(reset));
  Multiplexer #(.select(3), .width(16)) multiplexer_1 (
    .in0(R0_q), .in1(R1_q), .in2(R2_q), .in3(R3_q), .in4(R4_q), .in5(R5_q), .in6(R6_q), .in7(R7_q), .out(A),
    .sel(Addr_A));
  Multiplexer #(.select(3), .width(16)) multiplexer_2 (
    .in0(R0_q), .in1(R1_q), .in2(R2_q), .in3(R3_q), .in4(R4_q), .in5(R5_q), .in6(R6_q), .in7(R7_q), .out(B),
    .sel(Addr_B));
endmodule

module RegisterFileTester (
  output halt,
  output [15:0] A,
  output [15:0] B,
  output clk
);

  wire undriven;
  wire [2:0] Addr_A_data, Addr_B_data, Addr_C_data;
  wire [3:0] adder_1_out, addr_q;
  wire [15:0] C_data;

  Clock clock_1 (.out(clk));
  ROM #(.addrWidth(4), .dataWidth(3)) Addr_A (.addr(addr_q), .data(Addr_A_data));
  ROM #(.addrWidth(4), .dataWidth(3)) Addr_B (.addr(addr_q), .data(Addr_B_data));
  ROM #(.addrWidth(4), .dataWidth(3)) Addr_C (.addr(addr_q), .data(Addr_C_data));
  ROM #(.addrWidth(4), .dataWidth(1)) we (.addr(addr_q));  // open: data
  ROM #(.addrWidth(4), .dataWidth(16)) C (.addr(addr_q), .data(C_data));
  Adder #(.width(4)) adder_1 (.a(addr_q), .b(4'b0001), .out(adder_1_out), .cin(1'b0));  // open: cout
  Register #(.width(4)) addr (.D(adder_1_out), .en(1'b1), .clk(clk), .Q(addr_q), .clr(1'b0));
  Comparator #(.width(4)) comparator_1 (.a(addr_q), .b(4'b1111), .eq(halt));  // open: gt, lt
  RegisterFile registerfile_1 (
    .C(C_data), .Addr_C(Addr_C_data), .we(undriven), .Addr_B(Addr_B_data), .Addr_A(Addr_A_data), .clk(clk),
    .reset(1'b0), .A(A), .B(B));

  // Notes on the sheet:
  //   contents of Addr_A (hex, n*v repeats v):
  //   5 2 7 3 2 0 2 6 2 4 1 3 5 5 2 6
  //   contents of Addr_B (hex, n*v repeats v):
  //   4 4 6 0 2 3 5 5 5 0 0 4 5 3 7 5
  //   contents of Addr_C (hex, n*v repeats v):
  //   0 5 0 5 5 7 2 3 6 4 0 4 7 7 4 6
  //   contents of we (hex, n*v repeats v):
  //   0 0 0 1 0 0 1 0 0 0 1 1 0 0 1 1
  //   contents of C (hex, n*v repeats v):
  //   1 4 c f 0 5 9 7 c b 9 f b 9 1 e
endmodule

module LSL (
  input  [15:0] A,
  input  [15:0] B,
  output [15:0] LSLO
);

  wire multiplexer_1_out, multiplexer_2_out, multiplexer_3_out, multiplexer_4_out, multiplexer_5_out,
       multiplexer_6_out, multiplexer_7_out, multiplexer_8_out, multiplexer_9_out, multiplexer_10_out,
       multiplexer_11_out, multiplexer_12_out, multiplexer_13_out, multiplexer_14_out, multiplexer_15_out,
       multiplexer_16_out, multiplexer_17_out, multiplexer_18_out, multiplexer_19_out, multiplexer_20_out,
       multiplexer_21_out, multiplexer_22_out, multiplexer_23_out, multiplexer_24_out, multiplexer_25_out,
       multiplexer_26_out, multiplexer_27_out, multiplexer_28_out, multiplexer_29_out, multiplexer_30_out,
       multiplexer_31_out, multiplexer_32_out, multiplexer_33_out, multiplexer_34_out, multiplexer_35_out,
       multiplexer_36_out, multiplexer_37_out, multiplexer_38_out, multiplexer_39_out, multiplexer_40_out,
       multiplexer_41_out, multiplexer_42_out, multiplexer_43_out, multiplexer_44_out, multiplexer_45_out,
       multiplexer_46_out, multiplexer_47_out, multiplexer_48_out;

  Multiplexer multiplexer_1 (.in0(A[15]), .in1(A[14]), .out(multiplexer_1_out), .sel(B[0]));
  Multiplexer multiplexer_2 (.in0(A[14]), .in1(A[13]), .out(multiplexer_2_out), .sel(B[0]));
  Multiplexer multiplexer_3 (.in0(A[13]), .in1(A[12]), .out(multiplexer_3_out), .sel(B[0]));
  Multiplexer multiplexer_4 (.in0(A[12]), .in1(A[11]), .out(multiplexer_4_out), .sel(B[0]));
  Multiplexer multiplexer_5 (.in0(A[11]), .in1(A[10]), .out(multiplexer_5_out), .sel(B[0]));
  Multiplexer multiplexer_6 (.in0(A[10]), .in1(A[9]), .out(multiplexer_6_out), .sel(B[0]));
  Multiplexer multiplexer_7 (.in0(A[9]), .in1(A[8]), .out(multiplexer_7_out), .sel(B[0]));
  Multiplexer multiplexer_8 (.in0(A[8]), .in1(A[7]), .out(multiplexer_8_out), .sel(B[0]));
  Multiplexer multiplexer_9 (.in0(A[7]), .in1(A[6]), .out(multiplexer_9_out), .sel(B[0]));
  Multiplexer multiplexer_10 (.in0(A[6]), .in1(A[5]), .out(multiplexer_10_out), .sel(B[0]));
  Multiplexer multiplexer_11 (.in0(A[5]), .in1(A[4]), .out(multiplexer_11_out), .sel(B[0]));
  Multiplexer multiplexer_12 (.in0(A[4]), .in1(A[3]), .out(multiplexer_12_out), .sel(B[0]));
  Multiplexer multiplexer_13 (.in0(A[3]), .in1(A[2]), .out(multiplexer_13_out), .sel(B[0]));
  Multiplexer multiplexer_14 (.in0(A[2]), .in1(A[1]), .out(multiplexer_14_out), .sel(B[0]));
  Multiplexer multiplexer_15 (.in0(A[1]), .in1(A[0]), .out(multiplexer_15_out), .sel(B[0]));
  Multiplexer multiplexer_16 (.in0(A[0]), .in1(1'b0), .out(multiplexer_16_out), .sel(B[0]));
  Multiplexer multiplexer_17 (.in0(multiplexer_1_out), .in1(multiplexer_3_out), .out(multiplexer_17_out), .sel(B[1]));
  Multiplexer multiplexer_18 (.in0(multiplexer_2_out), .in1(multiplexer_4_out), .out(multiplexer_18_out), .sel(B[1]));
  Multiplexer multiplexer_19 (.in0(multiplexer_3_out), .in1(multiplexer_5_out), .out(multiplexer_19_out), .sel(B[1]));
  Multiplexer multiplexer_20 (.in0(multiplexer_4_out), .in1(multiplexer_6_out), .out(multiplexer_20_out), .sel(B[1]));
  Multiplexer multiplexer_21 (.in0(multiplexer_5_out), .in1(multiplexer_7_out), .out(multiplexer_21_out), .sel(B[1]));
  Multiplexer multiplexer_22 (.in0(multiplexer_6_out), .in1(multiplexer_8_out), .out(multiplexer_22_out), .sel(B[1]));
  Multiplexer multiplexer_23 (.in0(multiplexer_7_out), .in1(multiplexer_9_out), .out(multiplexer_23_out), .sel(B[1]));
  Multiplexer multiplexer_24 (.in0(multiplexer_8_out), .in1(multiplexer_10_out), .out(multiplexer_24_out), .sel(B[1]));
  Multiplexer multiplexer_25 (.in0(multiplexer_9_out), .in1(multiplexer_11_out), .out(multiplexer_25_out), .sel(B[1]));
  Multiplexer multiplexer_26 (.in0(multiplexer_10_out), .in1(multiplexer_12_out), .out(multiplexer_26_out), .sel(B[1]));
  Multiplexer multiplexer_27 (.in0(multiplexer_11_out), .in1(multiplexer_13_out), .out(multiplexer_27_out), .sel(B[1]));
  Multiplexer multiplexer_28 (.in0(multiplexer_12_out), .in1(multiplexer_14_out), .out(multiplexer_28_out), .sel(B[1]));
  Multiplexer multiplexer_29 (.in0(multiplexer_13_out), .in1(multiplexer_15_out), .out(multiplexer_29_out), .sel(B[1]));
  Multiplexer multiplexer_30 (.in0(multiplexer_14_out), .in1(multiplexer_16_out), .out(multiplexer_30_out), .sel(B[1]));
  Multiplexer multiplexer_31 (.in0(multiplexer_15_out), .in1(1'b0), .out(multiplexer_31_out), .sel(B[1]));
  Multiplexer multiplexer_32 (.in0(multiplexer_16_out), .in1(1'b0), .out(multiplexer_32_out), .sel(B[1]));
  Multiplexer multiplexer_33 (.in0(multiplexer_17_out), .in1(multiplexer_21_out), .out(multiplexer_33_out), .sel(B[2]));
  Multiplexer multiplexer_34 (.in0(multiplexer_18_out), .in1(multiplexer_22_out), .out(multiplexer_34_out), .sel(B[2]));
  Multiplexer multiplexer_35 (.in0(multiplexer_19_out), .in1(multiplexer_23_out), .out(multiplexer_35_out), .sel(B[2]));
  Multiplexer multiplexer_36 (.in0(multiplexer_20_out), .in1(multiplexer_24_out), .out(multiplexer_36_out), .sel(B[2]));
  Multiplexer multiplexer_37 (.in0(multiplexer_21_out), .in1(multiplexer_25_out), .out(multiplexer_37_out), .sel(B[2]));
  Multiplexer multiplexer_38 (.in0(multiplexer_22_out), .in1(multiplexer_26_out), .out(multiplexer_38_out), .sel(B[2]));
  Multiplexer multiplexer_39 (.in0(multiplexer_23_out), .in1(multiplexer_27_out), .out(multiplexer_39_out), .sel(B[2]));
  Multiplexer multiplexer_40 (.in0(multiplexer_24_out), .in1(multiplexer_28_out), .out(multiplexer_40_out), .sel(B[2]));
  Multiplexer multiplexer_41 (.in0(multiplexer_25_out), .in1(multiplexer_29_out), .out(multiplexer_41_out), .sel(B[2]));
  Multiplexer multiplexer_42 (.in0(multiplexer_26_out), .in1(multiplexer_30_out), .out(multiplexer_42_out), .sel(B[2]));
  Multiplexer multiplexer_43 (.in0(multiplexer_27_out), .in1(multiplexer_31_out), .out(multiplexer_43_out), .sel(B[2]));
  Multiplexer multiplexer_44 (.in0(multiplexer_28_out), .in1(multiplexer_32_out), .out(multiplexer_44_out), .sel(B[2]));
  Multiplexer multiplexer_45 (.in0(multiplexer_29_out), .in1(1'b0), .out(multiplexer_45_out), .sel(B[2]));
  Multiplexer multiplexer_46 (.in0(multiplexer_30_out), .in1(1'b0), .out(multiplexer_46_out), .sel(B[2]));
  Multiplexer multiplexer_47 (.in0(multiplexer_31_out), .in1(1'b0), .out(multiplexer_47_out), .sel(B[2]));
  Multiplexer multiplexer_48 (.in0(multiplexer_32_out), .in1(1'b0), .out(multiplexer_48_out), .sel(B[2]));
  Multiplexer multiplexer_49 (.in0(multiplexer_33_out), .in1(multiplexer_41_out), .out(LSLO[15]), .sel(B[3]));
  Multiplexer multiplexer_50 (.in0(multiplexer_34_out), .in1(multiplexer_42_out), .out(LSLO[14]), .sel(B[3]));
  Multiplexer multiplexer_51 (.in0(multiplexer_35_out), .in1(multiplexer_43_out), .out(LSLO[13]), .sel(B[3]));
  Multiplexer multiplexer_52 (.in0(multiplexer_36_out), .in1(multiplexer_44_out), .out(LSLO[12]), .sel(B[3]));
  Multiplexer multiplexer_53 (.in0(multiplexer_37_out), .in1(multiplexer_45_out), .out(LSLO[11]), .sel(B[3]));
  Multiplexer multiplexer_54 (.in0(multiplexer_38_out), .in1(multiplexer_46_out), .out(LSLO[10]), .sel(B[3]));
  Multiplexer multiplexer_55 (.in0(multiplexer_39_out), .in1(multiplexer_47_out), .out(LSLO[9]), .sel(B[3]));
  Multiplexer multiplexer_56 (.in0(multiplexer_40_out), .in1(multiplexer_48_out), .out(LSLO[8]), .sel(B[3]));
  Multiplexer multiplexer_57 (.in0(multiplexer_41_out), .in1(1'b0), .out(LSLO[7]), .sel(B[3]));
  Multiplexer multiplexer_58 (.in0(multiplexer_42_out), .in1(1'b0), .out(LSLO[6]), .sel(B[3]));
  Multiplexer multiplexer_59 (.in0(multiplexer_43_out), .in1(1'b0), .out(LSLO[5]), .sel(B[3]));
  Multiplexer multiplexer_60 (.in0(multiplexer_44_out), .in1(1'b0), .out(LSLO[4]), .sel(B[3]));
  Multiplexer multiplexer_61 (.in0(multiplexer_45_out), .in1(1'b0), .out(LSLO[3]), .sel(B[3]));
  Multiplexer multiplexer_62 (.in0(multiplexer_46_out), .in1(1'b0), .out(LSLO[2]), .sel(B[3]));
  Multiplexer multiplexer_63 (.in0(multiplexer_47_out), .in1(1'b0), .out(LSLO[1]), .sel(B[3]));
  Multiplexer multiplexer_64 (.in0(multiplexer_48_out), .in1(1'b0), .out(LSLO[0]), .sel(B[3]));
endmodule

module LSR (
  input  [15:0] A,
  input  [15:0] B,
  output [15:0] LSRO
);

  wire multiplexer_1_out, multiplexer_2_out, multiplexer_3_out, multiplexer_4_out, multiplexer_5_out,
       multiplexer_6_out, multiplexer_7_out, multiplexer_8_out, multiplexer_9_out, multiplexer_10_out,
       multiplexer_11_out, multiplexer_12_out, multiplexer_13_out, multiplexer_14_out, multiplexer_15_out,
       multiplexer_16_out, multiplexer_17_out, multiplexer_18_out, multiplexer_19_out, multiplexer_20_out,
       multiplexer_21_out, multiplexer_22_out, multiplexer_23_out, multiplexer_24_out, multiplexer_25_out,
       multiplexer_26_out, multiplexer_27_out, multiplexer_28_out, multiplexer_29_out, multiplexer_30_out,
       multiplexer_31_out, multiplexer_32_out, multiplexer_33_out, multiplexer_34_out, multiplexer_35_out,
       multiplexer_36_out, multiplexer_37_out, multiplexer_38_out, multiplexer_39_out, multiplexer_40_out,
       multiplexer_41_out, multiplexer_42_out, multiplexer_43_out, multiplexer_44_out, multiplexer_45_out,
       multiplexer_46_out, multiplexer_47_out, multiplexer_48_out;

  Multiplexer multiplexer_1 (.in0(A[0]), .in1(A[1]), .out(multiplexer_1_out), .sel(B[0]));
  Multiplexer multiplexer_2 (.in0(A[1]), .in1(A[2]), .out(multiplexer_2_out), .sel(B[0]));
  Multiplexer multiplexer_3 (.in0(A[2]), .in1(A[3]), .out(multiplexer_3_out), .sel(B[0]));
  Multiplexer multiplexer_4 (.in0(A[3]), .in1(A[4]), .out(multiplexer_4_out), .sel(B[0]));
  Multiplexer multiplexer_5 (.in0(A[4]), .in1(A[5]), .out(multiplexer_5_out), .sel(B[0]));
  Multiplexer multiplexer_6 (.in0(A[5]), .in1(A[6]), .out(multiplexer_6_out), .sel(B[0]));
  Multiplexer multiplexer_7 (.in0(A[6]), .in1(A[7]), .out(multiplexer_7_out), .sel(B[0]));
  Multiplexer multiplexer_8 (.in0(A[7]), .in1(A[8]), .out(multiplexer_8_out), .sel(B[0]));
  Multiplexer multiplexer_9 (.in0(A[8]), .in1(A[9]), .out(multiplexer_9_out), .sel(B[0]));
  Multiplexer multiplexer_10 (.in0(A[9]), .in1(A[10]), .out(multiplexer_10_out), .sel(B[0]));
  Multiplexer multiplexer_11 (.in0(A[10]), .in1(A[11]), .out(multiplexer_11_out), .sel(B[0]));
  Multiplexer multiplexer_12 (.in0(A[11]), .in1(A[12]), .out(multiplexer_12_out), .sel(B[0]));
  Multiplexer multiplexer_13 (.in0(A[12]), .in1(A[13]), .out(multiplexer_13_out), .sel(B[0]));
  Multiplexer multiplexer_14 (.in0(A[13]), .in1(A[14]), .out(multiplexer_14_out), .sel(B[0]));
  Multiplexer multiplexer_15 (.in0(A[14]), .in1(A[15]), .out(multiplexer_15_out), .sel(B[0]));
  Multiplexer multiplexer_16 (.in0(A[15]), .in1(1'b0), .out(multiplexer_16_out), .sel(B[0]));
  Multiplexer multiplexer_17 (.in0(multiplexer_1_out), .in1(multiplexer_3_out), .out(multiplexer_17_out), .sel(B[1]));
  Multiplexer multiplexer_18 (.in0(multiplexer_2_out), .in1(multiplexer_4_out), .out(multiplexer_18_out), .sel(B[1]));
  Multiplexer multiplexer_19 (.in0(multiplexer_3_out), .in1(multiplexer_5_out), .out(multiplexer_19_out), .sel(B[1]));
  Multiplexer multiplexer_20 (.in0(multiplexer_4_out), .in1(multiplexer_6_out), .out(multiplexer_20_out), .sel(B[1]));
  Multiplexer multiplexer_21 (.in0(multiplexer_5_out), .in1(multiplexer_7_out), .out(multiplexer_21_out), .sel(B[1]));
  Multiplexer multiplexer_22 (.in0(multiplexer_6_out), .in1(multiplexer_8_out), .out(multiplexer_22_out), .sel(B[1]));
  Multiplexer multiplexer_23 (.in0(multiplexer_7_out), .in1(multiplexer_9_out), .out(multiplexer_23_out), .sel(B[1]));
  Multiplexer multiplexer_24 (.in0(multiplexer_8_out), .in1(multiplexer_10_out), .out(multiplexer_24_out), .sel(B[1]));
  Multiplexer multiplexer_25 (.in0(multiplexer_9_out), .in1(multiplexer_11_out), .out(multiplexer_25_out), .sel(B[1]));
  Multiplexer multiplexer_26 (.in0(multiplexer_10_out), .in1(multiplexer_12_out), .out(multiplexer_26_out), .sel(B[1]));
  Multiplexer multiplexer_27 (.in0(multiplexer_11_out), .in1(multiplexer_13_out), .out(multiplexer_27_out), .sel(B[1]));
  Multiplexer multiplexer_28 (.in0(multiplexer_12_out), .in1(multiplexer_14_out), .out(multiplexer_28_out), .sel(B[1]));
  Multiplexer multiplexer_29 (.in0(multiplexer_13_out), .in1(multiplexer_15_out), .out(multiplexer_29_out), .sel(B[1]));
  Multiplexer multiplexer_30 (.in0(multiplexer_14_out), .in1(multiplexer_16_out), .out(multiplexer_30_out), .sel(B[1]));
  Multiplexer multiplexer_31 (.in0(multiplexer_15_out), .in1(1'b0), .out(multiplexer_31_out), .sel(B[1]));
  Multiplexer multiplexer_32 (.in0(multiplexer_16_out), .in1(1'b0), .out(multiplexer_32_out), .sel(B[1]));
  Multiplexer multiplexer_33 (.in0(multiplexer_17_out), .in1(multiplexer_21_out), .out(multiplexer_33_out), .sel(B[2]));
  Multiplexer multiplexer_34 (.in0(multiplexer_18_out), .in1(multiplexer_22_out), .out(multiplexer_34_out), .sel(B[2]));
  Multiplexer multiplexer_35 (.in0(multiplexer_19_out), .in1(multiplexer_23_out), .out(multiplexer_35_out), .sel(B[2]));
  Multiplexer multiplexer_36 (.in0(multiplexer_20_out), .in1(multiplexer_24_out), .out(multiplexer_36_out), .sel(B[2]));
  Multiplexer multiplexer_37 (.in0(multiplexer_21_out), .in1(multiplexer_25_out), .out(multiplexer_37_out), .sel(B[2]));
  Multiplexer multiplexer_38 (.in0(multiplexer_22_out), .in1(multiplexer_26_out), .out(multiplexer_38_out), .sel(B[2]));
  Multiplexer multiplexer_39 (.in0(multiplexer_23_out), .in1(multiplexer_27_out), .out(multiplexer_39_out), .sel(B[2]));
  Multiplexer multiplexer_40 (.in0(multiplexer_24_out), .in1(multiplexer_28_out), .out(multiplexer_40_out), .sel(B[2]));
  Multiplexer multiplexer_41 (.in0(multiplexer_25_out), .in1(multiplexer_29_out), .out(multiplexer_41_out), .sel(B[2]));
  Multiplexer multiplexer_42 (.in0(multiplexer_26_out), .in1(multiplexer_30_out), .out(multiplexer_42_out), .sel(B[2]));
  Multiplexer multiplexer_43 (.in0(multiplexer_27_out), .in1(multiplexer_31_out), .out(multiplexer_43_out), .sel(B[2]));
  Multiplexer multiplexer_44 (.in0(multiplexer_28_out), .in1(multiplexer_32_out), .out(multiplexer_44_out), .sel(B[2]));
  Multiplexer multiplexer_45 (.in0(multiplexer_29_out), .in1(1'b0), .out(multiplexer_45_out), .sel(B[2]));
  Multiplexer multiplexer_46 (.in0(multiplexer_30_out), .in1(1'b0), .out(multiplexer_46_out), .sel(B[2]));
  Multiplexer multiplexer_47 (.in0(multiplexer_31_out), .in1(1'b0), .out(multiplexer_47_out), .sel(B[2]));
  Multiplexer multiplexer_48 (.in0(multiplexer_32_out), .in1(1'b0), .out(multiplexer_48_out), .sel(B[2]));
  Multiplexer multiplexer_49 (.in0(multiplexer_33_out), .in1(multiplexer_41_out), .out(LSRO[0]), .sel(B[3]));
  Multiplexer multiplexer_50 (.in0(multiplexer_34_out), .in1(multiplexer_42_out), .out(LSRO[1]), .sel(B[3]));
  Multiplexer multiplexer_51 (.in0(multiplexer_35_out), .in1(multiplexer_43_out), .out(LSRO[2]), .sel(B[3]));
  Multiplexer multiplexer_52 (.in0(multiplexer_36_out), .in1(multiplexer_44_out), .out(LSRO[3]), .sel(B[3]));
  Multiplexer multiplexer_53 (.in0(multiplexer_37_out), .in1(multiplexer_45_out), .out(LSRO[4]), .sel(B[3]));
  Multiplexer multiplexer_54 (.in0(multiplexer_38_out), .in1(multiplexer_46_out), .out(LSRO[5]), .sel(B[3]));
  Multiplexer multiplexer_55 (.in0(multiplexer_39_out), .in1(multiplexer_47_out), .out(LSRO[6]), .sel(B[3]));
  Multiplexer multiplexer_56 (.in0(multiplexer_40_out), .in1(multiplexer_48_out), .out(LSRO[7]), .sel(B[3]));
  Multiplexer multiplexer_57 (.in0(multiplexer_41_out), .in1(1'b0), .out(LSRO[8]), .sel(B[3]));
  Multiplexer multiplexer_58 (.in0(multiplexer_42_out), .in1(1'b0), .out(LSRO[9]), .sel(B[3]));
  Multiplexer multiplexer_59 (.in0(multiplexer_43_out), .in1(1'b0), .out(LSRO[10]), .sel(B[3]));
  Multiplexer multiplexer_60 (.in0(multiplexer_44_out), .in1(1'b0), .out(LSRO[11]), .sel(B[3]));
  Multiplexer multiplexer_61 (.in0(multiplexer_45_out), .in1(1'b0), .out(LSRO[12]), .sel(B[3]));
  Multiplexer multiplexer_62 (.in0(multiplexer_46_out), .in1(1'b0), .out(LSRO[13]), .sel(B[3]));
  Multiplexer multiplexer_63 (.in0(multiplexer_47_out), .in1(1'b0), .out(LSRO[14]), .sel(B[3]));
  Multiplexer multiplexer_64 (.in0(multiplexer_48_out), .in1(1'b0), .out(LSRO[15]), .sel(B[3]));
endmodule

module ASR (
  input  [15:0] A,
  input  [15:0] B,
  output [15:0] ASRO
);

  wire multiplexer_1_out, multiplexer_2_out, multiplexer_3_out, multiplexer_4_out, multiplexer_5_out,
       multiplexer_6_out, multiplexer_7_out, multiplexer_8_out, multiplexer_9_out, multiplexer_10_out,
       multiplexer_11_out, multiplexer_12_out, multiplexer_13_out, multiplexer_14_out, multiplexer_15_out,
       multiplexer_16_out, multiplexer_17_out, multiplexer_18_out, multiplexer_19_out, multiplexer_20_out,
       multiplexer_21_out, multiplexer_22_out, multiplexer_23_out, multiplexer_24_out, multiplexer_25_out,
       multiplexer_26_out, multiplexer_27_out, multiplexer_28_out, multiplexer_29_out, multiplexer_30_out,
       multiplexer_31_out, multiplexer_32_out, multiplexer_33_out, multiplexer_34_out, multiplexer_35_out,
       multiplexer_36_out, multiplexer_37_out, multiplexer_38_out, multiplexer_39_out, multiplexer_40_out,
       multiplexer_41_out, multiplexer_42_out, multiplexer_43_out, multiplexer_44_out, multiplexer_45_out,
       multiplexer_46_out, multiplexer_47_out, multiplexer_48_out;

  Multiplexer multiplexer_1 (.in0(A[0]), .in1(A[1]), .out(multiplexer_1_out), .sel(B[0]));
  Multiplexer multiplexer_2 (.in0(A[1]), .in1(A[2]), .out(multiplexer_2_out), .sel(B[0]));
  Multiplexer multiplexer_3 (.in0(A[2]), .in1(A[3]), .out(multiplexer_3_out), .sel(B[0]));
  Multiplexer multiplexer_4 (.in0(A[3]), .in1(A[4]), .out(multiplexer_4_out), .sel(B[0]));
  Multiplexer multiplexer_5 (.in0(A[4]), .in1(A[5]), .out(multiplexer_5_out), .sel(B[0]));
  Multiplexer multiplexer_6 (.in0(A[5]), .in1(A[6]), .out(multiplexer_6_out), .sel(B[0]));
  Multiplexer multiplexer_7 (.in0(A[6]), .in1(A[7]), .out(multiplexer_7_out), .sel(B[0]));
  Multiplexer multiplexer_8 (.in0(A[7]), .in1(A[8]), .out(multiplexer_8_out), .sel(B[0]));
  Multiplexer multiplexer_9 (.in0(A[8]), .in1(A[9]), .out(multiplexer_9_out), .sel(B[0]));
  Multiplexer multiplexer_10 (.in0(A[9]), .in1(A[10]), .out(multiplexer_10_out), .sel(B[0]));
  Multiplexer multiplexer_11 (.in0(A[10]), .in1(A[11]), .out(multiplexer_11_out), .sel(B[0]));
  Multiplexer multiplexer_12 (.in0(A[11]), .in1(A[12]), .out(multiplexer_12_out), .sel(B[0]));
  Multiplexer multiplexer_13 (.in0(A[12]), .in1(A[13]), .out(multiplexer_13_out), .sel(B[0]));
  Multiplexer multiplexer_14 (.in0(A[13]), .in1(A[14]), .out(multiplexer_14_out), .sel(B[0]));
  Multiplexer multiplexer_15 (.in0(A[14]), .in1(A[15]), .out(multiplexer_15_out), .sel(B[0]));
  Multiplexer multiplexer_16 (.in0(A[15]), .in1(A[15]), .out(multiplexer_16_out), .sel(B[0]));
  Multiplexer multiplexer_17 (.in0(multiplexer_1_out), .in1(multiplexer_3_out), .out(multiplexer_17_out), .sel(B[1]));
  Multiplexer multiplexer_18 (.in0(multiplexer_2_out), .in1(multiplexer_4_out), .out(multiplexer_18_out), .sel(B[1]));
  Multiplexer multiplexer_19 (.in0(multiplexer_3_out), .in1(multiplexer_5_out), .out(multiplexer_19_out), .sel(B[1]));
  Multiplexer multiplexer_20 (.in0(multiplexer_4_out), .in1(multiplexer_6_out), .out(multiplexer_20_out), .sel(B[1]));
  Multiplexer multiplexer_21 (.in0(multiplexer_5_out), .in1(multiplexer_7_out), .out(multiplexer_21_out), .sel(B[1]));
  Multiplexer multiplexer_22 (.in0(multiplexer_6_out), .in1(multiplexer_8_out), .out(multiplexer_22_out), .sel(B[1]));
  Multiplexer multiplexer_23 (.in0(multiplexer_7_out), .in1(multiplexer_9_out), .out(multiplexer_23_out), .sel(B[1]));
  Multiplexer multiplexer_24 (.in0(multiplexer_8_out), .in1(multiplexer_10_out), .out(multiplexer_24_out), .sel(B[1]));
  Multiplexer multiplexer_25 (.in0(multiplexer_9_out), .in1(multiplexer_11_out), .out(multiplexer_25_out), .sel(B[1]));
  Multiplexer multiplexer_26 (.in0(multiplexer_10_out), .in1(multiplexer_12_out), .out(multiplexer_26_out), .sel(B[1]));
  Multiplexer multiplexer_27 (.in0(multiplexer_11_out), .in1(multiplexer_13_out), .out(multiplexer_27_out), .sel(B[1]));
  Multiplexer multiplexer_28 (.in0(multiplexer_12_out), .in1(multiplexer_14_out), .out(multiplexer_28_out), .sel(B[1]));
  Multiplexer multiplexer_29 (.in0(multiplexer_13_out), .in1(multiplexer_15_out), .out(multiplexer_29_out), .sel(B[1]));
  Multiplexer multiplexer_30 (.in0(multiplexer_14_out), .in1(multiplexer_16_out), .out(multiplexer_30_out), .sel(B[1]));
  Multiplexer multiplexer_31 (.in0(multiplexer_15_out), .in1(A[15]), .out(multiplexer_31_out), .sel(B[1]));
  Multiplexer multiplexer_32 (.in0(multiplexer_16_out), .in1(A[15]), .out(multiplexer_32_out), .sel(B[1]));
  Multiplexer multiplexer_33 (.in0(multiplexer_17_out), .in1(multiplexer_21_out), .out(multiplexer_33_out), .sel(B[2]));
  Multiplexer multiplexer_34 (.in0(multiplexer_18_out), .in1(multiplexer_22_out), .out(multiplexer_34_out), .sel(B[2]));
  Multiplexer multiplexer_35 (.in0(multiplexer_19_out), .in1(multiplexer_23_out), .out(multiplexer_35_out), .sel(B[2]));
  Multiplexer multiplexer_36 (.in0(multiplexer_20_out), .in1(multiplexer_24_out), .out(multiplexer_36_out), .sel(B[2]));
  Multiplexer multiplexer_37 (.in0(multiplexer_21_out), .in1(multiplexer_25_out), .out(multiplexer_37_out), .sel(B[2]));
  Multiplexer multiplexer_38 (.in0(multiplexer_22_out), .in1(multiplexer_26_out), .out(multiplexer_38_out), .sel(B[2]));
  Multiplexer multiplexer_39 (.in0(multiplexer_23_out), .in1(multiplexer_27_out), .out(multiplexer_39_out), .sel(B[2]));
  Multiplexer multiplexer_40 (.in0(multiplexer_24_out), .in1(multiplexer_28_out), .out(multiplexer_40_out), .sel(B[2]));
  Multiplexer multiplexer_41 (.in0(multiplexer_25_out), .in1(multiplexer_29_out), .out(multiplexer_41_out), .sel(B[2]));
  Multiplexer multiplexer_42 (.in0(multiplexer_26_out), .in1(multiplexer_30_out), .out(multiplexer_42_out), .sel(B[2]));
  Multiplexer multiplexer_43 (.in0(multiplexer_27_out), .in1(multiplexer_31_out), .out(multiplexer_43_out), .sel(B[2]));
  Multiplexer multiplexer_44 (.in0(multiplexer_28_out), .in1(multiplexer_32_out), .out(multiplexer_44_out), .sel(B[2]));
  Multiplexer multiplexer_45 (.in0(multiplexer_29_out), .in1(A[15]), .out(multiplexer_45_out), .sel(B[2]));
  Multiplexer multiplexer_46 (.in0(multiplexer_30_out), .in1(A[15]), .out(multiplexer_46_out), .sel(B[2]));
  Multiplexer multiplexer_47 (.in0(multiplexer_31_out), .in1(A[15]), .out(multiplexer_47_out), .sel(B[2]));
  Multiplexer multiplexer_48 (.in0(multiplexer_32_out), .in1(A[15]), .out(multiplexer_48_out), .sel(B[2]));
  Multiplexer multiplexer_49 (.in0(multiplexer_33_out), .in1(multiplexer_41_out), .out(ASRO[0]), .sel(B[3]));
  Multiplexer multiplexer_50 (.in0(multiplexer_34_out), .in1(multiplexer_42_out), .out(ASRO[1]), .sel(B[3]));
  Multiplexer multiplexer_51 (.in0(multiplexer_35_out), .in1(multiplexer_43_out), .out(ASRO[2]), .sel(B[3]));
  Multiplexer multiplexer_52 (.in0(multiplexer_36_out), .in1(multiplexer_44_out), .out(ASRO[3]), .sel(B[3]));
  Multiplexer multiplexer_53 (.in0(multiplexer_37_out), .in1(multiplexer_45_out), .out(ASRO[4]), .sel(B[3]));
  Multiplexer multiplexer_54 (.in0(multiplexer_38_out), .in1(multiplexer_46_out), .out(ASRO[5]), .sel(B[3]));
  Multiplexer multiplexer_55 (.in0(multiplexer_39_out), .in1(multiplexer_47_out), .out(ASRO[6]), .sel(B[3]));
  Multiplexer multiplexer_56 (.in0(multiplexer_40_out), .in1(multiplexer_48_out), .out(ASRO[7]), .sel(B[3]));
  Multiplexer multiplexer_57 (.in0(multiplexer_41_out), .in1(A[15]), .out(ASRO[8]), .sel(B[3]));
  Multiplexer multiplexer_58 (.in0(multiplexer_42_out), .in1(A[15]), .out(ASRO[9]), .sel(B[3]));
  Multiplexer multiplexer_59 (.in0(multiplexer_43_out), .in1(A[15]), .out(ASRO[10]), .sel(B[3]));
  Multiplexer multiplexer_60 (.in0(multiplexer_44_out), .in1(A[15]), .out(ASRO[11]), .sel(B[3]));
  Multiplexer multiplexer_61 (.in0(multiplexer_45_out), .in1(A[15]), .out(ASRO[12]), .sel(B[3]));
  Multiplexer multiplexer_62 (.in0(multiplexer_46_out), .in1(A[15]), .out(ASRO[13]), .sel(B[3]));
  Multiplexer multiplexer_63 (.in0(multiplexer_47_out), .in1(A[15]), .out(ASRO[14]), .sel(B[3]));
  Multiplexer multiplexer_64 (.in0(multiplexer_48_out), .in1(A[15]), .out(ASRO[15]), .sel(B[3]));
endmodule

module FSM (
  input  CLK,
  input  [1:0] OP,
  input  Branch,
  output ir_we,
  output pc_we,
  output ra_we,
  output rb_we,
  output rz_we,
  output rd_we,
  output rw_we,
  output rf_we,
  output Mem_write
);

  wire and_1_out, decoder_1_out0, decoder_1_out2, decoder_1_out3, decoder_2_out5, decoder_2_out6, or_1_out,
       or_2_out, register_2_q;
  wire [2:0] adder_1_out, register_1_q;

  Register #(.width(3)) register_1 (.D(adder_1_out), .clk(CLK), .Q(register_1_q), .clr(or_1_out));  // open: en
  or or_1 (or_1_out, and_1_out, decoder_2_out6);
  Decoder #(.enable("false"), .select(2)) decoder_1 (
    .out0(decoder_1_out0), .out2(decoder_1_out2), .out3(decoder_1_out3), .sel(OP));  // open: out1
  Register #(.width(1)) register_2 (.D(Branch), .clk(CLK), .Q(register_2_q));  // open: en, clr
  and and_1 (and_1_out, rw_we, register_2_q);
  Adder #(.width(3)) adder_1 (.a(register_1_q), .b(3'b001), .out(adder_1_out));  // open: cin, cout
  Decoder #(.enable("false"), .select(3)) decoder_2 (
    .out1(ir_we), .out2(ra_we), .out3(rd_we), .out4(rw_we), .out5(decoder_2_out5), .out6(decoder_2_out6),
    .sel(adder_1_out));  // open: out0, out7
  or or_2 (or_2_out, decoder_1_out0, decoder_1_out2);
  or or_3 (pc_we, Branch, ir_we);
  and and_2 (rf_we, decoder_2_out5, or_2_out);
  and and_3 (Mem_write, rw_we, decoder_1_out3);

  assign rb_we = ra_we;
  assign rz_we = rd_we;
endmodule

module ZNV (
  input  [2:0] Conditon,
  input  Z,
  input  N,
  input  V,
  output Result
);

  wire and_1_out, and_2_out, and_3_out, and_4_out, and_5_out, and_6_out, decoder_1_out0, decoder_1_out1,
       decoder_1_out2, decoder_1_out3, decoder_1_out4, decoder_1_out5, not_1_out, or_1_out, xnor_1_out,
       xor_1_out, xor_2_out;

  Decoder #(.enable("false"), .select(3)) decoder_1 (
    .out0(decoder_1_out0), .out1(decoder_1_out1), .out2(decoder_1_out2), .out3(decoder_1_out3),
    .out4(decoder_1_out4), .out5(decoder_1_out5), .sel(Conditon));  // open: out6, out7
  xor xor_1 (xor_1_out, N, V);
  xnor xnor_1 (xnor_1_out, N, V);
  and and_1 (and_1_out, decoder_1_out0, Z);
  not not_1 (not_1_out, Z);
  and and_2 (and_2_out, decoder_1_out2, xor_1_out);
  and and_3 (and_3_out, decoder_1_out3, or_1_out);
  or or_1 (or_1_out, Z, xor_1_out);
  and and_4 (and_4_out, decoder_1_out1, not_1_out);
  and and_5 (and_5_out, decoder_1_out5, xnor_1_out);
  and and_6 (and_6_out, decoder_1_out4, xor_2_out);
  xor xor_2 (xor_2_out, Z, xnor_1_out);
  or or_2 (Result, and_1_out, and_4_out, and_2_out, and_3_out, and_6_out, and_5_out);
endmodule
