// Logisim project cpuqasim.circ as structural Verilog: 5 circuits, main circuit CPU
module CPU (
  output [47:0] cpu_out,
  output halt
);

  wire alu_1_carry, alu_1_negative, alu_1_overflow, alu_1_zero, and_1_out, and_2_out, and_3_out, and_4_out,
       and_5_out, and_6_out, and_7_out, and_8_out, and_9_out, and_10_out, and_11_out, and_12_out, clk_out,
       multiplexer_4_out, multiplexer_7_out, multiplexer_9_out, multiplexer_10_out, nor_1_out, not_1_out,
       or_1_out, or_2_out, reset_out, xnor_1_out, xor_1_out;
  wire [2:0] counter_1_q, multiplexer_3_out, multiplexer_5_out, multiplexer_6_out, multiplexer_12_out,
       undriven, undriven_2;
  wire [15:0] adder_1_out, alu_1_c, bit_extender_1_out, bit_extender_2_out, InsMem_data, multiplexer_1_out,
       multiplexer_2_out, multiplexer_8_out, multiplexer_11_out, RA_q, ram_1_dout, RD_q, register_1_q,
       registerfile_1_a, registerfile_1_b, RW_q;

  assign bit_extender_1_out = {{13{cpu_out[25]}}, cpu_out[25:23]};  // Bit_Extender bit_extender_1
  Multiplexer #(.width(16)) multiplexer_1 (
    .in0(16'h1), .in1(bit_extender_1_out), .out(multiplexer_1_out), .sel(and_1_out));
  and and_1 (and_1_out, and_9_out, and_2_out);
  and and_2 (and_2_out, and_9_out, and_3_out);
  Clock clk (.out(clk_out));
  Button reset (.out(reset_out));
  Counter #(.max('h4), .width(3)) counter_1 (
    .clr(reset_out), .load(and_2_out), .clk(clk_out), .D(3'b000), .Q(counter_1_q));  // open: up, count, carry
  and and_3 (and_3_out, ~counter_1_q[0], counter_1_q[1], ~counter_1_q[2]);  // AND_Gate
  Register #(.width(16)) PC (.D(adder_1_out), .en(or_1_out), .clk(clk_out), .Q(cpu_out[47:32]), .clr(reset_out));
  or or_1 (or_1_out, and_2_out, nor_1_out);
  nor nor_1 (nor_1_out, counter_1_q[0], counter_1_q[1], counter_1_q[2]);
  and and_4 (and_4_out, counter_1_q[0], ~counter_1_q[1], ~counter_1_q[2]);  // AND_Gate
  and and_5 (and_5_out, ~counter_1_q[0], counter_1_q[1], ~counter_1_q[2]);  // AND_Gate
  and and_6 (and_6_out, ~counter_1_q[2], counter_1_q[1], counter_1_q[0]);  // AND_Gate
  Adder #(.width(16)) adder_1 (.a(cpu_out[47:32]), .b(multiplexer_1_out), .out(adder_1_out));  // open: cin, cout
  and and_7 (and_7_out, and_8_out, not_1_out);
  and and_8 (and_8_out, ~counter_1_q[0], ~counter_1_q[1], counter_1_q[2]);  // AND_Gate
  ROM #(.addrWidth(16), .dataWidth(16)) InsMem (.addr(cpu_out[47:32]), .data(InsMem_data));
  Register #(.width(16)) RA (.D(registerfile_1_a), .en(and_4_out), .clk(clk_out), .Q(RA_q), .clr(reset_out));
  RegisterFile registerfile_1 (
    .Addr_A(multiplexer_3_out), .Addr_B(multiplexer_5_out), .Addr_C(multiplexer_6_out), .we(and_7_out),
    .clk(clk_out), .reset(reset_out), .C(multiplexer_8_out), .A(registerfile_1_a), .B(registerfile_1_b));
  Register #(.width(16)) register_1 (
    .D(registerfile_1_b), .en(and_4_out), .clk(clk_out), .Q(register_1_q), .clr(reset_out));
  Multiplexer #(.width(16)) multiplexer_2 (
    .in0(register_1_q), .in1(multiplexer_11_out), .out(multiplexer_2_out), .sel(multiplexer_10_out));
  Register #(.width(16)) IR (.D(InsMem_data), .en(nor_1_out), .clk(clk_out), .Q(cpu_out[31:16]), .clr(reset_out));
  ALU alu_1 (
    .A(RA_q), .B(multiplexer_2_out), .fun(multiplexer_12_out), .overflow(alu_1_overflow), .zero(alu_1_zero),
    .C(alu_1_c), .negative(alu_1_negative), .carry(alu_1_carry));
  not not_1 (not_1_out, cpu_out[30]);
  Register #(.width(16)) RZ (.D(alu_1_c), .en(and_5_out), .clk(clk_out), .Q(cpu_out[15:0]), .clr(reset_out));
  Register #(.width(16)) RD (.D(register_1_q), .en(and_5_out), .clk(clk_out), .Q(RD_q), .clr(reset_out));
  Register #(.width(16)) RW (.D(cpu_out[15:0]), .en(and_6_out), .clk(clk_out), .Q(RW_q), .clr(reset_out));
  Comparator #(.width(16)) comparator_1 (.a(cpu_out[31:16]), .b(16'h4380), .eq(halt));  // open: gt, lt
  Multiplexer #(.select(2), .width(3)) multiplexer_3 (
    .in0(cpu_out[22:20]), .in1(cpu_out[22:20]), .in2(cpu_out[22:20]), .in3(cpu_out[22:20]),
    .out(multiplexer_3_out), .sel(cpu_out[31:30]));
  Multiplexer #(.select(2)) multiplexer_4 (
    .in3(and_6_out), .out(multiplexer_4_out), .sel(cpu_out[31:30]));  // open: in0, in1, in2
  Multiplexer #(.select(2), .width(3)) multiplexer_5 (
    .in0(cpu_out[18:16]), .in1(cpu_out[18:16]), .in2(cpu_out[18:16]), .in3(cpu_out[25:23]),
    .out(multiplexer_5_out), .sel(cpu_out[31:30]));
  Multiplexer #(.select(2), .width(3)) multiplexer_6 (
    .in0(cpu_out[25:23]), .in1(undriven), .in2(cpu_out[25:23]), .in3(undriven_2), .out(multiplexer_6_out),
    .sel(cpu_out[31:30]));
  and and_9 (and_9_out, multiplexer_9_out, multiplexer_7_out);
  Multiplexer #(.select(2)) multiplexer_7 (
    .in0(1'b0), .in1(1'b1), .in2(1'b0), .in3(1'b0), .out(multiplexer_7_out), .sel(cpu_out[31:30]));
  Multiplexer #(.select(2), .width(16)) multiplexer_8 (
    .in0(RW_q), .in2(ram_1_dout), .out(multiplexer_8_out), .sel(cpu_out[31:30]));  // open: in1, in3
  Multiplexer #(.select(3)) multiplexer_9 (
    .in0(and_10_out), .in1(and_11_out), .in2(xor_1_out), .in3(or_2_out), .in4(and_12_out), .in5(xnor_1_out),
    .out(multiplexer_9_out), .sel(cpu_out[29:27]));  // open: in6, in7
  and and_10 (and_10_out, alu_1_zero, alu_1_zero);
  RAM #(.addrWidth(16), .dataWidth(16), .enables("line")) ram_1 (
    .addr(cpu_out[15:0]), .we(multiplexer_4_out), .clk(clk_out), .din(RD_q), .dout(ram_1_dout));
  Multiplexer #(.select(2)) multiplexer_10 (
    .in0(cpu_out[26]), .in1(cpu_out[26]), .in2(cpu_out[26]), .in3(1'b1), .out(multiplexer_10_out),
    .sel(cpu_out[31:30]));
  assign bit_extender_2_out = {{12{cpu_out[19]}}, cpu_out[19:16]};  // Bit_Extender bit_extender_2
  and and_11 (and_11_out, ~alu_1_zero, ~alu_1_zero);  // AND_Gate
  Multiplexer #(.select(2), .width(16)) multiplexer_11 (
    .in0(bit_extender_2_out), .in1(bit_extender_2_out), .in2(bit_extender_2_out), .in3(bit_extender_2_out),
    .out(multiplexer_11_out), .sel(cpu_out[31:30]));
  xor xor_1 (xor_1_out, alu_1_negative, alu_1_overflow);
  Multiplexer #(.select(2), .width(3)) multiplexer_12 (
    .in0(cpu_out[29:27]), .in1(3'b001), .in2(cpu_out[29:27]), .in3(cpu_out[29:27]), .out(multiplexer_12_out),
    .sel(cpu_out[31:30]));
  or or_2 (or_2_out, and_10_out, xor_1_out);
  and and_12 (and_12_out, and_11_out, xnor_1_out);
  xnor xnor_1 (xnor_1_out, alu_1_negative, alu_1_overflow);

  // Notes on the sheet:
  //   want 2/010
  //   1
  //   1f. ir_we = pc_we = !(a + b + c)
  //   0
  //   2
  //   2d. ra_we = rb_we = !a * !b * c
  //   3e. rz_we = rd_we = !a * b * !c
  //   4m. rw_we = !a * b * c 
  //   5w. rf_we = a * !b * !c
  //   contents of InsMem (hex, n*v repeats v):
  //   493 6d90 2091 491 401 52d 6da0 2122 521 401 15b0 16d0 1621 4540 4e50 1b1 2c91 4e50 3521 2d2 4e50
  //   4d01 21b3 5b1 5b0 4380
  //   V
  //   C
  //   Z
  //   N
  //   3-0
  //   6-4
  //   9-7
  //   10
  //   13-11
  //   V
  //   C
  //   Z
  //   N
  //   Addr_A
  //   Addr_B
  //   WE_RAM
  //   Addr_C
  //   is branching
  //   C
  //   3-0
  //   6-4
  //   9-7
  //   10
  //   13-11
  //   check branch condition
  //   equal Z==1
  //   V
  //   C
  //   Z
  //   N
  //   I
  //   not equal Z==0 
  //   ImmV
  //   V
  //   C
  //   Z
  //   N
  //   signed less than N!=V 
  //   sub when branch >
  //   3-0
  //   6-4
  //   9-7
  //   10
  //   13-11
  //   Fun
  //   V
  //   C
  //   Z
  //   N
  //   signed less or equal (Z==1) or (N!=V) 
  //   signed greater than (Z==0) and (N==V) 
  //   V
  //   C
  //   Z
  //   N
  //   signed greater or equal N==V 
  //   V
  //   C
  //   Z
  //   N
  //   V
  //   C
  //   Z
  //   N
endmodule

module ALU (
  input  [15:0] A,
  input  [15:0] B,
  input  [2:0] fun,
  output overflow,
  output carry,
  output [15:0] C,
  output negative,
  output zero
);

  wire adder_1_cout, and_2_out, and_3_out, and_4_out;
  wire [14:0] adder_1_out;
  wire [15:0] and_1_out, bit_extender_1_out, nor_1_out, or_1_out, shifter_1_out, shifter_2_out,
       shifter_3_out, xor_1_out;
  wire [15:15] xor_2_out;

  assign bit_extender_1_out = {{15{fun[0]}}, fun[0]};  // Bit_Extender bit_extender_1
  assign xor_1_out = bit_extender_1_out ^ B;  // XOR_Gate xor_1, 16 bits wide
  assign and_1_out = A & B;  // AND_Gate and_1, 16 bits wide
  assign or_1_out = A | B;  // OR_Gate or_1, 16 bits wide
  assign nor_1_out = ~(A | B);  // NOR_Gate nor_1, 16 bits wide
  Shifter #(.width(16)) shifter_1 (.in(A), .\dist (B[3:0]), .out(shifter_1_out));
  Shifter #(.shift("lr"), .width(16)) shifter_2 (.in(A), .\dist (B[3:0]), .out(shifter_2_out));
  Shifter #(.shift("ar"), .width(16)) shifter_3 (.in(A), .\dist (B[3:0]), .out(shifter_3_out));
  Adder #(.width(15)) adder_1 (.a(A[14:0]), .b(xor_1_out[14:0]), .out(adder_1_out), .cin(fun[0]), .cout(adder_1_cout));
  xor xor_2 (xor_2_out[15], adder_1_cout, A[15], xor_1_out[15]);
  Multiplexer #(.select(3), .width(16)) multiplexer_1 (
    .in0({xor_2_out[15], adder_1_out}), .in1({xor_2_out[15], adder_1_out}), .in2(and_1_out), .in3(or_1_out),
    .in4(nor_1_out), .in5(shifter_1_out), .in6(shifter_2_out), .in7(shifter_3_out), .out(C), .sel(fun));
  and and_2 (and_2_out, A[15], adder_1_cout);
  and and_3 (and_3_out, xor_1_out[15], adder_1_cout);
  and and_4 (and_4_out, A[15], xor_1_out[15]);
  or or_2 (carry, and_2_out, and_3_out, and_4_out);
  xor xor_3 (overflow, adder_1_cout, carry);
  nor nor_2 (zero, C[0], C[1], C[2], C[3], C[4], C[5], C[6], C[7], C[8], C[9], C[10], C[11], C[12], C[13], C[14], C[15]);

  assign negative = C[15];
endmodule

module RegisterFile (
  input  [2:0] Addr_A,
  input  [2:0] Addr_B,
  input  [2:0] Addr_C,
  input  we,
  input  clk,
  input  reset,
  input  [15:0] C,
  output [15:0] A,
  output [15:0] B
);

  wire and_1_out, and_2_out, and_3_out, and_4_out, and_5_out, and_6_out, and_7_out, and_8_out,
       decoder_1_out0, decoder_1_out1, decoder_1_out2, decoder_1_out3, decoder_1_out4, decoder_1_out5,
       decoder_1_out6, decoder_1_out7;
  wire [15:0] R0_q, R1_q, R2_q, R3_q, R4_q, R5_q, R6_q, R7_q;

  Decoder #(.select(3)) decoder_1 (
    .out0(decoder_1_out0), .out1(decoder_1_out1), .out2(decoder_1_out2), .out3(decoder_1_out3),
    .out4(decoder_1_out4), .out5(decoder_1_out5), .out6(decoder_1_out6), .out7(decoder_1_out7), .sel(Addr_C));  // open: en
  Register #(.width(16)) R0 (.D(C), .en(and_1_out), .clk(clk), .Q(R0_q), .clr(reset));
  and and_1 (and_1_out, decoder_1_out0, we);
  Register #(.width(16)) R1 (.D(C), .en(and_2_out), .clk(clk), .Q(R1_q), .clr(reset));
  and and_2 (and_2_out, decoder_1_out1, we);
  Register #(.width(16)) R2 (.D(C), .en(and_3_out), .clk(clk), .Q(R2_q), .clr(reset));
  and and_3 (and_3_out, decoder_1_out2, we);
  Register #(.width(16)) R3 (.D(C), .en(and_4_out), .clk(clk), .Q(R3_q), .clr(reset));
  and and_4 (and_4_out, decoder_1_out3, we);
  Register #(.width(16)) R4 (.D(C), .en(and_5_out), .clk(clk), .Q(R4_q), .clr(reset));
  and and_5 (and_5_out, decoder_1_out4, we);
  Register #(.width(16)) R5 (.D(C), .en(and_6_out), .clk(clk), .Q(R5_q), .clr(reset));
  and and_6 (and_6_out, decoder_1_out5, we);
  Register #(.width(16)) R6 (.D(C), .en(and_7_out), .clk(clk), .Q(R6_q), .clr(reset));
  and and_7 (and_7_out, decoder_1_out6, we);
  Register #(.width(16)) R7 (.D(C), .en(and_8_out), .clk(clk), .Q(R7_q), .clr(reset));
  and and_8 (and_8_out, decoder_1_out7, we);
  Multiplexer #(.select(3), .width(16)) multiplexer_1 (
    .in0(R0_q), .in1(R1_q), .in2(R2_q), .in3(R3_q), .in4(R4_q), .in5(R5_q), .in6(R6_q), .in7(R7_q), .out(A),
    .sel(Addr_A));
  Multiplexer #(.select(3), .width(16)) multiplexer_2 (
    .in0(R0_q), .in1(R1_q), .in2(R2_q), .in3(R3_q), .in4(R4_q), .in5(R5_q), .in6(R6_q), .in7(R7_q), .out(B),
    .sel(Addr_B));
endmodule

module RegisterFileTester (
  output halt,
  output [15:0] A,
  output [15:0] B,
  output clk
);

  wire undriven;
  wire [2:0] Addr_A_data, Addr_B_data, Addr_C_data;
  wire [3:0] adder_1_out, addr_q;
  wire [15:0] C_data;

  Clock clock_1 (.out(clk));
  ROM #(.addrWidth(4), .dataWidth(3)) Addr_A (.addr(addr_q), .data(Addr_A_data));
  ROM #(.addrWidth(4), .dataWidth(3)) Addr_B (.addr(addr_q), .data(Addr_B_data));
  ROM #(.addrWidth(4), .dataWidth(3)) Addr_C (.addr(addr_q), .data(Addr_C_data));
  ROM #(.addrWidth(4), .dataWidth(1)) we (.addr(addr_q));  // open: data
  ROM #(.addrWidth(4), .dataWidth(16)) C (.addr(addr_q), .data(C_data));
  Adder #(.width(4)) adder_1 (.a(addr_q), .b(4'b0001), .out(adder_1_out), .cin(1'b0));  // open: cout
  Register #(.width(4)) addr (.D(adder_1_out), .en(1'b1), .clk(clk), .Q(addr_q), .clr(1'b0));
  Comparator #(.width(4)) comparator_1 (.a(addr_q), .b(4'b1111), .eq(halt));  // open: gt, lt
  RegisterFile registerfile_1 (
    .Addr_A(Addr_A_data), .Addr_B(Addr_B_data), .Addr_C(Addr_C_data), .we(undriven), .clk(clk), .reset(1'b0),
    .C(C_data), .A(A), .B(B));

  // Notes on the sheet:
  //   contents of Addr_A (hex, n*v repeats v):
  //   5 2 7 3 2 0 2 6 2 4 1 3 5 5 2 6
  //   contents of Addr_B (hex, n*v repeats v):
  //   4 4 6 0 2 3 5 5 5 0 0 4 5 3 7 5
  //   contents of Addr_C (hex, n*v repeats v):
  //   0 5 0 5 5 7 2 3 6 4 0 4 7 7 4 6
  //   contents of we (hex, n*v repeats v):
  //   0 0 0 1 0 0 1 0 0 0 1 1 0 0 1 1
  //   contents of C (hex, n*v repeats v):
  //   1 4 c f 0 5 9 7 c b 9 f b 9 1 e
endmodule

module SUB_GX (
  output [47:0] cpu_out,
  output halt
);

  wire alu_1_carry, alu_1_negative, alu_1_overflow, alu_1_zero, and_1_out, and_2_out, and_3_out, and_4_out,
       and_5_out, and_6_out, and_7_out, and_8_out, and_9_out, and_10_out, and_11_out, and_12_out, clk_out,
       multiplexer_4_out, multiplexer_7_out, multiplexer_9_out, multiplexer_10_out, nor_1_out, not_1_out,
       or_1_out, or_2_out, reset_out, xnor_1_out, xor_1_out;
  wire [2:0] counter_1_q, multiplexer_3_out, multiplexer_5_out, multiplexer_6_out, multiplexer_12_out,
       undriven, undriven_2;
  wire [15:0] adder_1_out, alu_1_c, bit_extender_1_out, bit_extender_2_out, InsMem_data, multiplexer_1_out,
       multiplexer_2_out, multiplexer_8_out, multiplexer_11_out, RA_q, ram_1_dout, RD_q, register_1_q,
       registerfile_1_a, registerfile_1_b, RW_q;

  assign bit_extender_1_out = {{13{cpu_out[25]}}, cpu_out[25:23]};  // Bit_Extender bit_extender_1
  Multiplexer #(.width(16)) multiplexer_1 (
    .in0(16'h1), .in1(bit_extender_1_out), .out(multiplexer_1_out), .sel(and_1_out));
  and and_1 (and_1_out, and_9_out, and_2_out);
  Clock clk (.out(clk_out));
  Button reset (.out(reset_out));
  and and_2 (and_2_out, and_9_out, and_3_out);
  Counter #(.max('h4), .width(3)) counter_1 (
    .clr(reset_out), .load(and_2_out), .clk(clk_out), .D(3'b000), .Q(counter_1_q));  // open: up, count, carry
  and and_3 (and_3_out, ~counter_1_q[0], counter_1_q[1], ~counter_1_q[2]);  // AND_Gate
  nor nor_1 (nor_1_out, counter_1_q[0], counter_1_q[1], counter_1_q[2]);
  Register #(.width(16)) PC (.D(adder_1_out), .en(or_1_out), .clk(clk_out), .Q(cpu_out[47:32]), .clr(reset_out));
  or or_1 (or_1_out, and_2_out, nor_1_out);
  and and_4 (and_4_out, counter_1_q[0], ~counter_1_q[1], ~counter_1_q[2]);  // AND_Gate
  and and_5 (and_5_out, ~counter_1_q[0], counter_1_q[1], ~counter_1_q[2]);  // AND_Gate
  and and_6 (and_6_out, ~counter_1_q[2], counter_1_q[1], counter_1_q[0]);  // AND_Gate
  Adder #(.width(16)) adder_1 (.a(cpu_out[47:32]), .b(multiplexer_1_out), .out(adder_1_out));  // open: cin, cout
  ROM #(.addrWidth(16), .dataWidth(16)) InsMem (.addr(cpu_out[47:32]), .data(InsMem_data));
  and and_7 (and_7_out, and_8_out, not_1_out);
  and and_8 (and_8_out, ~counter_1_q[0], ~counter_1_q[1], counter_1_q[2]);  // AND_Gate
  Register #(.width(16)) RA (.D(registerfile_1_a), .en(and_4_out), .clk(clk_out), .Q(RA_q), .clr(reset_out));
  RegisterFile registerfile_1 (
    .Addr_A(multiplexer_3_out), .Addr_B(multiplexer_5_out), .Addr_C(multiplexer_6_out), .we(and_7_out),
    .clk(clk_out), .reset(reset_out), .C(multiplexer_8_out), .A(registerfile_1_a), .B(registerfile_1_b));
  Register #(.width(16)) register_1 (
    .D(registerfile_1_b), .en(and_4_out), .clk(clk_out), .Q(register_1_q), .clr(reset_out));
  Multiplexer #(.width(16)) multiplexer_2 (
    .in0(register_1_q), .in1(multiplexer_11_out), .out(multiplexer_2_out), .sel(multiplexer_10_out));
  Register #(.width(16)) IR (.D(InsMem_data), .en(nor_1_out), .clk(clk_out), .Q(cpu_out[31:16]), .clr(reset_out));
  ALU alu_1 (
    .A(RA_q), .B(multiplexer_2_out), .fun(multiplexer_12_out), .overflow(alu_1_overflow), .zero(alu_1_zero),
    .C(alu_1_c), .negative(alu_1_negative), .carry(alu_1_carry));
  not not_1 (not_1_out, cpu_out[30]);
  Register #(.width(16)) RZ (.D(alu_1_c), .en(and_5_out), .clk(clk_out), .Q(cpu_out[15:0]), .clr(reset_out));
  Register #(.width(16)) RD (.D(register_1_q), .en(and_5_out), .clk(clk_out), .Q(RD_q), .clr(reset_out));
  Register #(.width(16)) RW (.D(cpu_out[15:0]), .en(and_6_out), .clk(clk_out), .Q(RW_q), .clr(reset_out));
  Comparator #(.width(16)) comparator_1 (.a(cpu_out[31:16]), .b(16'h4380), .eq(halt));  // open: gt, lt
  Multiplexer #(.select(2), .width(3)) multiplexer_3 (
    .in0(cpu_out[22:20]), .in1(cpu_out[22:20]), .in2(cpu_out[22:20]), .in3(cpu_out[22:20]),
    .out(multiplexer_3_out), .sel(cpu_out[31:30]));
  Multiplexer #(.select(2)) multiplexer_4 (
    .in3(and_6_out), .out(multiplexer_4_out), .sel(cpu_out[31:30]));  // open: in0, in1, in2
  Multiplexer #(.select(2), .width(3)) multiplexer_5 (
    .in0(cpu_out[18:16]), .in1(cpu_out[18:16]), .in2(cpu_out[18:16]), .in3(cpu_out[25:23]),
    .out(multiplexer_5_out), .sel(cpu_out[31:30]));
  Multiplexer #(.select(2), .width(3)) multiplexer_6 (
    .in0(cpu_out[25:23]), .in1(undriven), .in2(cpu_out[25:23]), .in3(undriven_2), .out(multiplexer_6_out),
    .sel(cpu_out[31:30]));
  and and_9 (and_9_out, multiplexer_9_out, multiplexer_7_out);
  Multiplexer #(.select(2)) multiplexer_7 (
    .in0(1'b0), .in1(1'b1), .in2(1'b0), .in3(1'b0), .out(multiplexer_7_out), .sel(cpu_out[31:30]));
  Multiplexer #(.select(2), .width(16)) multiplexer_8 (
    .in0(RW_q), .in2(ram_1_dout), .out(multiplexer_8_out), .sel(cpu_out[31:30]));  // open: in1, in3
  Multiplexer #(.select(3)) multiplexer_9 (
    .in0(and_10_out), .in1(and_11_out), .in2(xor_1_out), .in3(or_2_out), .in4(and_12_out), .in5(xnor_1_out),
    .out(multiplexer_9_out), .sel(cpu_out[29:27]));  // open: in6, in7
  RAM #(.addrWidth(16), .dataWidth(16), .enables("line")) ram_1 (
    .addr(cpu_out[15:0]), .we(multiplexer_4_out), .clk(clk_out), .din(RD_q), .dout(ram_1_dout));
  and and_10 (and_10_out, alu_1_zero, alu_1_zero);
  Multiplexer #(.select(2)) multiplexer_10 (
    .in0(cpu_out[26]), .in1(cpu_out[26]), .in2(cpu_out[26]), .in3(1'b1), .out(multiplexer_10_out),
    .sel(cpu_out[31:30]));
  assign bit_extender_2_out = {{12{cpu_out[19]}}, cpu_out[19:16]};  // Bit_Extender bit_extender_2
  and and_11 (and_11_out, ~alu_1_zero, ~alu_1_zero);  // AND_Gate
  Multiplexer #(.select(2), .width(16)) multiplexer_11 (
    .in0(bit_extender_2_out), .in1(bit_extender_2_out), .in2(bit_extender_2_out), .in3(bit_extender_2_out),
    .out(multiplexer_11_out), .sel(cpu_out[31:30]));
  xor xor_1 (xor_1_out, alu_1_negative, alu_1_overflow);
  Multiplexer #(.select(2), .width(3)) multiplexer_12 (
    .in0(cpu_out[29:27]), .in1(3'b001), .in2(cpu_out[29:27]), .in3(cpu_out[29:27]), .out(multiplexer_12_out),
    .sel(cpu_out[31:30]));
  or or_2 (or_2_out, and_10_out, xor_1_out);
  and and_12 (and_12_out, and_11_out, xnor_1_out);
  xnor xnor_1 (xnor_1_out, alu_1_negative, alu_1_overflow);

  // Notes on the sheet:
  //   want 2/010
  //   0
  //   1
  //   2
  //   1f. ir_we = pc_we = !(a + b + c)
  //   2d. ra_we = rb_we = !a * !b * c
  //   3e. rz_we = rd_we = !a * b * !c
  //   4m. rw_we = !a * b * c 
  //   5w. rf_we = a * !b * !c
  //   V
  //   C
  //   Z
  //   N
  //   3-0
  //   6-4
  //   9-7
  //   10
  //   13-11
  //   V
  //   C
  //   Z
  //   N
  //   Addr_A
  //   WE_RAM
  //   Addr_B
  //   Addr_C
  //   is branching
  //   C
  //   3-0
  //   6-4
  //   9-7
  //   10
  //   13-11
  //   check branch condition
  //   equal Z==1
  //   V
  //   C
  //   Z
  //   N
  //   I
  //   not equal Z==0 
  //   ImmV
  //   V
  //   C
  //   Z
  //   N
  //   signed less than N!=V 
  //   sub when branch >
  //   3-0
  //   6-4
  //   9-7
  //   10
  //   13-11
  //   Fun
  //   V
  //   C
  //   Z
  //   N
  //   signed less or equal (Z==1) or (N!=V) 
  //   signed greater than (Z==0) and (N==V) 
  //   V
  //   C
  //   Z
  //   N
  //   signed greater or equal N==V 
  //   V
  //   C
  //   Z
  //   N
  //   V
  //   C
  //   Z
  //   N
endmodule
